// Logisim project Pedro_Carvalho_651230_05.circ as structural Verilog: 1 circuit, main circuit main
module main (
  input  Clear
);

  wire clock_1_out, j_k_ff_1_qn, j_k_ff_2_qn;

  Clock clock_1 (.out(clock_1_out));
  J_K_Flip_Flop j_k_ff_1 (.J(1'b1), .clk(clock_1_out), .K(1'b1), .Qn(j_k_ff_1_qn), .reset(Clear));  // open: Q, preset
  J_K_Flip_Flop j_k_ff_2 (.clk(j_k_ff_1_qn), .Qn(j_k_ff_2_qn), .reset(Clear));  // open: J, K, Q, preset
  J_K_Flip_Flop j_k_ff_3 (.J(1'b1), .clk(j_k_ff_2_qn), .K(1'b1), .reset(Clear));  // open: Q, Qn, preset

  // Notes on the sheet:
  //   Mat: 651230
  //   Prova 2 - Extra 05
  //   Pedro Henrique Lima Carvalho
endmodule
