// Logisim project Pedro_Carvalho_651230_B1.circ as structural Verilog: 1 circuit, main circuit main
module main (
  input  in_1
);

  wire and_1_out, clock_1_out, d_ff_1_qn, j_k_ff_1_q, s_r_ff_1_q, s_r_ff_1_qn;

  Clock clock_1 (.out(clock_1_out));
  and and_1 (and_1_out, j_k_ff_1_q, d_ff_1_qn);
  D_Flip_Flop d_ff_1 (.clk(clock_1_out), .D(and_1_out), .Qn(d_ff_1_qn), .reset(in_1));  // open: Q, preset
  J_K_Flip_Flop j_k_ff_1 (
    .J(s_r_ff_1_q), .clk(clock_1_out), .K(s_r_ff_1_q), .Q(j_k_ff_1_q), .reset(in_1));  // open: Qn, preset
  S_R_Flip_Flop s_r_ff_1 (
    .S(s_r_ff_1_qn), .clk(clock_1_out), .R(1'b0), .Q(s_r_ff_1_q), .Qn(s_r_ff_1_qn), .reset(in_1));  // open: preset

  // Notes on the sheet:
  //   Mat: 651230
  //   Prova 2 - B1
  //   Pedro Henrique Lima Carvalho
endmodule
