// Logisim project Pedro_Carvalho_B1.circ as structural Verilog: 1 circuit, main circuit main
module main (
);

  wire and_1_out, and_2_out, and_3_out, and_4_out, and_5_out, and_6_out, and_7_out, and_8_out, and_9_out,
       and_10_out, and_11_out, and_12_out, and_13_out, and_14_out, and_15_out, D_Q, D_Q_prime, JK_Q,
       JK_Q_prime, or_1_out, or_2_out, or_3_out, SR_Q, SR_Q_prime, X_out;

  Clock X (.out(X_out));
  and and_1 (and_1_out, D_Q_prime, JK_Q, SR_Q);
  and and_2 (and_2_out, D_Q, JK_Q_prime, SR_Q_prime);
  and and_3 (and_3_out, D_Q, JK_Q_prime, SR_Q);
  and and_4 (and_4_out, D_Q, JK_Q_prime, SR_Q);
  and and_5 (and_5_out, D_Q, JK_Q, SR_Q_prime);
  and and_6 (and_6_out, D_Q_prime, JK_Q_prime, SR_Q);
  and and_7 (and_7_out, D_Q_prime, JK_Q, SR_Q_prime);
  and and_8 (and_8_out, D_Q_prime, JK_Q, SR_Q);
  and and_9 (and_9_out, D_Q, JK_Q_prime, SR_Q);
  and and_10 (and_10_out, D_Q, JK_Q, SR_Q_prime);
  and and_11 (and_11_out, D_Q, JK_Q, SR_Q);
  and and_12 (and_12_out, D_Q_prime, JK_Q_prime, SR_Q_prime);
  and and_13 (and_13_out, D_Q_prime, JK_Q, SR_Q_prime);
  and and_14 (and_14_out, D_Q, JK_Q_prime, SR_Q_prime);
  and and_15 (and_15_out, D_Q, JK_Q, SR_Q_prime);
  or or_1 (or_1_out, and_1_out, and_2_out, and_3_out, and_4_out, and_5_out);
  or or_2 (or_2_out, and_6_out, and_7_out, and_8_out, and_9_out, and_10_out, and_11_out);
  or or_3 (or_3_out, and_12_out, and_13_out, and_14_out, and_15_out);
  D_Flip_Flop d_ff_1 (.clk(X_out), .D(or_1_out), .Q(D_Q), .Qn(D_Q_prime));  // open: preset, reset
  J_K_Flip_Flop j_k_ff_1 (.J(or_2_out), .clk(X_out), .K(or_2_out), .Q(JK_Q), .Qn(JK_Q_prime));  // open: preset, reset
  S_R_Flip_Flop s_r_ff_1 (.S(or_3_out), .clk(X_out), .R(1'b0), .Q(SR_Q), .Qn(SR_Q_prime));  // open: preset, reset

  // Notes on the sheet:
  //   Mat: 651230
  //   Prova 2 - B1
  //   Pedro Henrique Lima Carvalho
endmodule
