// Logisim project Pedro_Carvalho_651230_questao_03.circ as structural Verilog: 1 circuit, main circuit main
module main (
  input  x,
  input  y,
  input  z,
  output a,
  output a__simp,
  output b,
  output b__simpl,
  output c,
  output c__simpl,
  output d,
  output d__simpl,
  output e,
  output e__simpl
);

  wire and_1_out, and_3_out, and_5_out, and_7_out, and_8_out, and_10_out, and_11_out, and_12_out, not_1_out,
       not_2_out, not_3_out, not_4_out, not_5_out, not_6_out, not_7_out, or_1_out, or_2_out, or_3_out,
       or_4_out, or_6_out, or_7_out;

  not not_1 (not_1_out, x);
  not not_2 (not_2_out, y);
  not not_3 (not_3_out, z);
  and and_1 (and_1_out, not_1_out, not_3_out);
  or or_1 (or_1_out, and_1_out, y);
  or or_2 (or_2_out, not_2_out, z);
  not not_4 (not_4_out, or_2_out);
  or or_3 (or_3_out, x, not_2_out);
  and and_2 (b, or_3_out, and_3_out);
  and and_3 (and_3_out, z, not_2_out);
  and and_4 (b__simpl, z, not_2_out);
  or or_4 (or_4_out, not_2_out, z);
  not not_5 (not_5_out, or_4_out);
  and and_5 (and_5_out, y, x);
  not not_6 (not_6_out, and_5_out);
  and and_6 (c__simpl, y, not_3_out, not_1_out);
  and and_7 (and_7_out, y, z);
  not not_7 (not_7_out, and_7_out);
  and and_8 (and_8_out, not_3_out, x);
  or or_5 (d__simpl, not_2_out, not_3_out);
  or or_6 (or_6_out, not_1_out, not_2_out);
  and and_9 (e, or_6_out, or_7_out);
  or or_7 (or_7_out, y, not_3_out);
  and and_10 (and_10_out, not_1_out, y);
  or or_8 (e__simpl, and_10_out, and_11_out, and_12_out);
  and and_11 (and_11_out, not_1_out, not_3_out);
  and and_12 (and_12_out, not_2_out, not_3_out);
  and and_13 (a, or_1_out, not_4_out);
  and and_14 (a__simp, y, not_3_out);
  and and_15 (c, not_5_out, not_6_out);
  or or_9 (d, not_7_out, and_8_out);

  // Notes on the sheet:
  //   Pedro Henrique Lima Carvalho
  //   Recuperacao 1 - Exercicio 3
  //   Arquitetura de Computadores I - Pucminas
  //   ?
endmodule
