// Logisim project Pedro_Carvalho_651230_questao_04.circ as structural Verilog: 1 circuit, main circuit main
module main (
  input  w,
  input  x,
  input  y,
  input  z,
  input  x_2,
  input  y_2,
  input  w_2,
  input  z_2,
  output a,
  output d,
  output b,
  output c,
  output c_2
);

  wire and_1_out, and_2_out, and_3_out, and_4_out, and_5_out, and_6_out, and_7_out, and_8_out, and_9_out,
       and_10_out, and_11_out, and_12_out, and_13_out, and_14_out, and_15_out, and_16_out, and_17_out,
       and_18_out, and_19_out, and_20_out, and_21_out, and_22_out, and_23_out, and_24_out, and_25_out,
       and_26_out, and_27_out, and_28_out, and_29_out, and_30_out, and_31_out, not_1_out, not_2_out,
       not_3_out, not_4_out, not_5_out, not_6_out, not_7_out, not_8_out;

  not not_1 (not_1_out, x);
  not not_2 (not_2_out, y);
  not not_3 (not_3_out, z);
  not not_4 (not_4_out, w);
  and and_1 (and_1_out, not_1_out, not_2_out, not_3_out);
  and and_2 (and_2_out, not_1_out, y, not_3_out);
  and and_3 (and_3_out, not_1_out, y, z);
  and and_4 (and_4_out, x, y, not_3_out);
  and and_5 (and_5_out, x, y, z);
  and and_6 (and_6_out, not_1_out, not_2_out, not_3_out);
  and and_7 (and_7_out, not_1_out, not_2_out, z);
  and and_8 (and_8_out, not_1_out, y, z);
  and and_9 (and_9_out, x, not_2_out, not_3_out);
  and and_10 (and_10_out, x, y, not_3_out);
  and and_11 (and_11_out, not_1_out, not_2_out, not_4_out, not_3_out);
  and and_12 (and_12_out, not_1_out, not_2_out, not_4_out, z);
  and and_13 (and_13_out, not_1_out, not_2_out, w, not_3_out);
  and and_14 (and_14_out, not_1_out, not_2_out, w, z);
  and and_15 (and_15_out, not_1_out, y, not_4_out, not_3_out);
  and and_16 (and_16_out, not_1_out, y, w, z);
  and and_17 (and_17_out, x, not_2_out, w, z);
  and and_18 (and_18_out, x, y, not_4_out, z);
  or or_1 (a, and_1_out, and_2_out, and_3_out, and_4_out, and_5_out);
  or or_2 (b, and_6_out, and_7_out, and_8_out, and_9_out, and_10_out);
  or or_3 (c_2, and_11_out, and_12_out, and_13_out, and_14_out, and_15_out, and_16_out, and_17_out, and_18_out);
  not not_5 (not_5_out, y_2);
  not not_6 (not_6_out, x_2);
  not not_7 (not_7_out, w_2);
  not not_8 (not_8_out, z_2);
  and and_19 (and_19_out, not_6_out, not_5_out, not_7_out, not_8_out);
  and and_20 (and_20_out, not_6_out, not_5_out, w_2, z_2);
  and and_21 (and_21_out, x_2, not_5_out, w_2, not_8_out);
  and and_22 (and_22_out, not_6_out, not_5_out, not_7_out, z_2);
  and and_23 (and_23_out, not_6_out, y_2, not_7_out, z_2);
  and and_24 (and_24_out, x_2, not_5_out, w_2, z_2);
  and and_25 (and_25_out, not_6_out, not_5_out, w_2, not_8_out);
  and and_26 (and_26_out, not_6_out, y_2, w_2, not_8_out);
  and and_27 (and_27_out, x_2, y_2, w_2, not_8_out);
  and and_28 (and_28_out, not_6_out, not_5_out, not_7_out, not_8_out);
  and and_29 (and_29_out, not_6_out, not_5_out, w_2, not_8_out);
  and and_30 (and_30_out, not_6_out, y_2, w_2, z_2);
  and and_31 (and_31_out, x_2, y_2, w_2, not_8_out);
  or or_4 (d, and_19_out, and_25_out, and_20_out, and_26_out, and_21_out, and_27_out);
  or or_5 (c, and_28_out, and_22_out, and_29_out, and_23_out, and_30_out, and_24_out, and_31_out);

  // Notes on the sheet:
  //   Pedro Henrique Lima Carvalho
  //   Recuperacao 1 - Exercicio 4
  //   Arquitetura de Computadores I - Pucminas
endmodule
