// Logisim project Pedro_Carvalho_651230_questao_05.circ as structural Verilog: 1 circuit, main circuit main
module main (
  input  w,
  input  x,
  input  y,
  input  z,
  input  x_2,
  input  y_2,
  input  w_2,
  input  z_2,
  output a,
  output d,
  output b,
  output c,
  output e
);

  wire not_1_out, not_2_out, not_3_out, not_4_out, not_5_out, not_6_out, not_7_out, not_8_out, or_1_out,
       or_2_out, or_3_out, or_4_out, or_5_out, or_6_out, or_7_out, or_8_out, or_9_out, or_10_out, or_11_out,
       or_12_out, or_13_out, or_14_out, or_15_out, or_16_out, or_17_out, or_18_out, or_19_out, or_20_out,
       or_21_out, or_22_out;

  not not_1 (not_1_out, x);
  not not_2 (not_2_out, y);
  not not_3 (not_3_out, w);
  not not_4 (not_4_out, z);
  or or_1 (or_1_out, x, y, not_4_out);
  or or_2 (or_2_out, x, not_2_out, z);
  or or_3 (or_3_out, not_1_out, y, z);
  or or_4 (or_4_out, not_1_out, y, not_4_out);
  or or_5 (or_5_out, x, y, not_4_out);
  or or_6 (or_6_out, x, not_2_out, z);
  or or_7 (or_7_out, not_1_out, not_2_out, z);
  or or_8 (or_8_out, not_1_out, not_2_out, not_4_out);
  or or_9 (or_9_out, x, not_2_out, not_3_out, not_4_out);
  or or_10 (or_10_out, not_1_out, y, w, not_4_out);
  or or_11 (or_11_out, not_1_out, y, not_3_out, not_4_out);
  or or_12 (or_12_out, not_1_out, not_2_out, w, z);
  and and_1 (a, or_1_out, or_2_out, or_3_out, or_4_out);
  and and_2 (b, or_5_out, or_6_out, or_7_out, or_8_out);
  and and_3 (c, or_9_out, or_10_out, or_11_out, or_12_out);
  not not_5 (not_5_out, y_2);
  not not_6 (not_6_out, x_2);
  not not_7 (not_7_out, w_2);
  not not_8 (not_8_out, z_2);
  or or_13 (or_13_out, x_2, y_2, not_7_out, z_2);
  or or_14 (or_14_out, x_2, not_5_out, w_2, z_2);
  or or_15 (or_15_out, x_2, not_5_out, not_7_out, z_2);
  or or_16 (or_16_out, x_2, not_5_out, not_7_out, not_8_out);
  or or_17 (or_17_out, not_6_out, y_2, not_7_out, z_2);
  or or_18 (or_18_out, x_2, y_2, not_7_out, not_8_out);
  or or_19 (or_19_out, x_2, not_5_out, w_2, not_8_out);
  or or_20 (or_20_out, x_2, not_5_out, not_7_out, not_8_out);
  or or_21 (or_21_out, not_6_out, y_2, not_7_out, not_8_out);
  or or_22 (or_22_out, not_6_out, not_5_out, not_7_out, not_8_out);
  and and_4 (d, or_13_out, or_14_out, or_15_out, or_16_out, or_17_out);
  and and_5 (e, or_18_out, or_19_out, or_20_out, or_21_out, or_22_out);

  // Notes on the sheet:
  //   Pedro Henrique Lima Carvalho
  //   Recuperacao 1 - Exercicio 5
  //   Arquitetura de Computadores I - Pucminas
endmodule
