// Logisim project Pedro_Carvalho_651230_questao_10.circ as structural Verilog: 1 circuit, main circuit main
module main (
  input  x,
  input  y,
  input  x_2,
  input  y_2,
  input  x_3,
  input  y_3,
  input  z,
  input  x_4,
  input  y_4,
  input  z_2,
  output S2,
  output S1,
  output S0,
  output S2_2,
  output S1_2,
  output S0_2,
  output S2_3,
  output S1_3,
  output S0_3,
  output S2_4,
  output S1_4,
  output S0_4
);

  wire and_1_out, and_2_out, and_3_out, and_4_out, and_5_out, and_6_out, and_7_out, and_8_out, and_9_out,
       and_10_out, and_11_out, and_12_out, and_13_out, and_14_out, and_15_out, and_16_out, and_17_out,
       and_18_out, and_19_out, not_1_out, not_2_out, not_3_out, not_4_out, not_5_out, not_6_out, not_7_out,
       not_8_out, not_9_out, not_10_out, or_7_out, or_8_out, or_9_out, or_10_out, or_12_out, or_13_out,
       or_14_out, or_15_out, or_16_out, or_17_out, or_18_out, or_19_out, or_20_out, or_21_out, or_22_out,
       or_23_out;

  not not_1 (not_1_out, x);
  not not_2 (not_2_out, x_3);
  not not_3 (not_3_out, y);
  not not_4 (not_4_out, y_3);
  and and_1 (and_1_out, not_1_out, not_3_out);
  and and_2 (and_2_out, x, not_3_out);
  and and_3 (and_3_out, not_1_out, not_3_out);
  and and_4 (and_4_out, x, y);
  and and_5 (and_5_out, not_1_out, y);
  and and_6 (and_6_out, x, not_3_out);
  and and_7 (and_7_out, x, y);
  not not_5 (not_5_out, z);
  and and_8 (and_8_out, not_2_out, not_4_out, z);
  and and_9 (and_9_out, not_2_out, y_3, not_5_out);
  and and_10 (and_10_out, x_3, not_4_out, z);
  and and_11 (and_11_out, x_3, y_3, not_5_out);
  and and_12 (and_12_out, not_2_out, y_3, not_5_out);
  and and_13 (and_13_out, not_2_out, y_3, z);
  and and_14 (and_14_out, x_3, not_4_out, not_5_out);
  and and_15 (and_15_out, x_3, not_4_out, z);
  and and_16 (and_16_out, x_3, not_4_out, not_5_out);
  and and_17 (and_17_out, x_3, not_4_out, z);
  and and_18 (and_18_out, x_3, y_3, not_5_out);
  and and_19 (and_19_out, x_3, y_3, z);
  or or_1 (S0, and_1_out, and_2_out);
  or or_2 (S1, and_3_out, and_4_out);
  or or_3 (S2, and_5_out, and_6_out, and_7_out);
  or or_4 (S0_3, and_8_out, and_9_out, and_10_out, and_11_out);
  or or_5 (S1_3, and_12_out, and_13_out, and_14_out, and_15_out);
  or or_6 (S2_3, and_16_out, and_17_out, and_18_out, and_19_out);
  not not_6 (not_6_out, x_2);
  not not_7 (not_7_out, y_2);
  not not_8 (not_8_out, x_4);
  not not_9 (not_9_out, y_4);
  or or_7 (or_7_out, x_2, not_7_out);
  and and_20 (S0_2, or_7_out, or_8_out);
  or or_8 (or_8_out, not_6_out, not_7_out);
  or or_9 (or_9_out, x_2, not_7_out);
  and and_21 (S1_2, or_9_out, or_10_out);
  or or_10 (or_10_out, not_6_out, y_2);
  or or_11 (S2_2, x_2, y_2);
  not not_10 (not_10_out, z_2);
  or or_12 (or_12_out, x_4, y_4, z_2);
  or or_13 (or_13_out, x_4, not_9_out, not_10_out);
  and and_22 (S0_4, or_12_out, or_13_out, or_14_out, or_15_out);
  or or_14 (or_14_out, not_8_out, y_4, z_2);
  or or_15 (or_15_out, not_8_out, not_9_out, not_10_out);
  or or_16 (or_16_out, x_4, y_4, z_2);
  or or_17 (or_17_out, x_4, y_4, not_10_out);
  and and_23 (S1_4, or_16_out, or_17_out, or_18_out, or_19_out);
  or or_18 (or_18_out, not_8_out, not_9_out, z_2);
  or or_19 (or_19_out, not_8_out, not_9_out, not_10_out);
  or or_20 (or_20_out, x_4, y_4, z_2);
  or or_21 (or_21_out, x_4, y_4, not_10_out);
  and and_24 (S2_4, or_20_out, or_21_out, or_22_out, or_23_out);
  or or_22 (or_22_out, x_4, not_9_out, z_2);
  or or_23 (or_23_out, x_4, not_9_out, not_10_out);

  // Notes on the sheet:
  //   Pedro Henrique Lima Carvalho
  //   Recuperacao 1 - Exercicio 10
  //   Arquitetura de Computadores I - Pucminas
  //   Excesso 3 - Mintermos
  //   Código Gray - Mintermos
  //   Excesso 3 - Maxtermos
  //   Código Gray - Maxtermos
endmodule
