// Logisim project Pedro_Henrique_Lima_Carvalho_651230_ex_C1_C2.circ as structural Verilog: 1 circuit, main circuit main
module main (
  input  [7:0] C1,
  input  [7:0] C2,
  output [7:0] out_3,
  output [7:0] out_4
);

  wire [7:0] not_2_out;

  assign out_3 = ~C1;  // NOT_Gate not_1, 8 bits wide
  assign not_2_out = ~C2;  // NOT_Gate not_2, 8 bits wide
  Adder adder_1 (.a(not_2_out), .b(8'h1), .out(out_4));  // open: cin, cout
endmodule
