// Logisim project Pedro_Henrique_Lima_Carvalho_651230_Guia05.circ as structural Verilog: 1 circuit, main circuit main
module main (
  input  x,
  input  y,
  output Exemplo_1,
  output Exemplo_2,
  output Exemplo_3,
  output Exemplo_4,
  output Exemplo_5,
  output Exemplo_6,
  output Exemplo_7,
  output Exemplo_8,
  output Exemplo_9
);

  wire nand_1_out, nand_2_out, nand_3_out, nand_4_out, nand_5_out, nand_6_out, nand_9_out, nand_11_out,
       nor_1_out, nor_2_out, nor_3_out, nor_4_out, nor_5_out, nor_6_out, nor_7_out, nor_10_out, nor_12_out,
       nor_14_out, not_1_out;

  not not_1 (not_1_out, x);
  and and_1 (Exemplo_1, not_1_out, y);
  nand nand_1 (nand_1_out, x, x);
  nand nand_2 (nand_2_out, y, y);
  nor nor_1 (nor_1_out, x, x);
  nor nor_2 (nor_2_out, y, y);
  nand nand_3 (nand_3_out, x, y);
  nor nor_3 (nor_3_out, x, y);
  nand nand_4 (nand_4_out, x, x);
  nand nand_5 (nand_5_out, y, y);
  nor nor_4 (nor_4_out, x, x);
  nor nor_5 (nor_5_out, y, y);
  nand nand_6 (nand_6_out, x, x);
  nor nor_6 (nor_6_out, x, x);
  nor nor_7 (nor_7_out, y, y);
  nand nand_7 (Exemplo_2, nand_1_out, nand_2_out);
  nor nor_8 (Exemplo_3, nor_1_out, nor_2_out);
  nand nand_8 (Exemplo_4, nand_3_out, nand_3_out);
  nor nor_9 (Exemplo_5, nor_3_out, nor_3_out);
  nand nand_9 (nand_9_out, y, nand_4_out);
  nand nand_10 (Exemplo_6, nand_9_out, nand_11_out);
  nand nand_11 (nand_11_out, nand_5_out, x);
  nor nor_10 (nor_10_out, y, nor_4_out);
  nor nor_11 (Exemplo_7, nor_10_out, nor_12_out);
  nor nor_12 (nor_12_out, nor_5_out, x);
  nand nand_12 (Exemplo_8, nand_6_out, y);
  nor nor_13 (Exemplo_9, nor_14_out, nor_14_out);
  nor nor_14 (nor_14_out, nor_6_out, nor_7_out);
endmodule
