// Logisim project Pedro_Henrique_Lima_Carvalho_651230_guia06_10.circ as structural Verilog: 1 circuit, main circuit main
module main (
  input  x,
  input  y,
  input  w,
  input  z,
  output out_5,
  output out_6
);

  wire and_1_out, and_2_out, and_3_out, not_1_out, not_2_out, not_3_out, not_4_out, not_5_out, not_6_out,
       not_7_out, not_8_out, not_9_out, not_10_out, not_11_out, or_1_out, or_2_out, or_3_out, or_4_out,
       or_5_out;

  not not_1 (not_1_out, y);
  not not_2 (not_2_out, x);
  not not_3 (not_3_out, w);
  and and_1 (and_1_out, z, w, y);
  not not_4 (not_4_out, x);
  not not_5 (not_5_out, y);
  not not_6 (not_6_out, y);
  not not_7 (not_7_out, w);
  not not_8 (not_8_out, z);
  or or_1 (or_1_out, not_1_out, w, not_2_out);
  not not_9 (not_9_out, or_1_out);
  and and_2 (and_2_out, y, x);
  not not_10 (not_10_out, and_2_out);
  or or_2 (or_2_out, and_1_out, not_4_out);
  or or_3 (or_3_out, x, y);
  or or_4 (or_4_out, x, not_5_out);
  or or_5 (or_5_out, not_6_out, not_7_out, not_8_out);
  and and_3 (and_3_out, not_9_out, not_10_out);
  or or_6 (out_5, and_3_out, not_11_out);
  not not_11 (not_11_out, or_2_out);
  and and_4 (out_6, or_3_out, or_4_out, or_5_out);

  // Notes on the sheet:
  //   Pedro Henrique Lima Carvalho
  //   Arq 1 - Tarde
  //   Mat: 651230
  //   Guia 06 Ex. 10
  //   Circuito Completo
  //   Circuito Simplificado
endmodule
