// Logisim project Pedro_Henrique_Lima_Carvalho_651230_Exemplo_0701.circ as structural Verilog: 1 circuit, main circuit main
module main (
  input  A,
  input  B,
  input  Select,
  output s_and,
  output s_or
);

  wire and_1_out, not_1_out, or_1_out;

  and and_1 (and_1_out, A, B);
  or or_1 (or_1_out, A, B);
  and and_2 (s_and, and_1_out, not_1_out);
  not not_1 (not_1_out, Select);
  and and_3 (s_or, Select, or_1_out);

  // Notes on the sheet:
  //   Turno: tarde
  //   Mat: 651230
  //   Arquitetura de Computadores 1
  //   Pedro Herique Lima Carvalho
  //   Exemplo_0701
endmodule
