// Logisim project Pedro_Henrique_Lima_Carvalho_651230_Exemplo_0703.circ as structural Verilog: 1 circuit, main circuit main
module main (
  input  A,
  input  B,
  input  Select,
  input  Select_2,
  output S
);

  wire and_1_out, and_2_out, and_3_out, and_4_out, and_5_out, and_6_out, and_7_out, nand_1_out, nor_1_out,
       not_1_out, not_2_out, not_3_out, or_1_out, or_2_out, or_3_out;

  and and_1 (and_1_out, A, B);
  or or_1 (or_1_out, A, B);
  nand nand_1 (nand_1_out, A, B);
  nor nor_1 (nor_1_out, A, B);
  and and_2 (and_2_out, and_1_out, not_1_out);
  not not_1 (not_1_out, Select);
  and and_3 (and_3_out, Select, or_1_out);
  and and_4 (and_4_out, nand_1_out, not_2_out);
  not not_2 (not_2_out, Select);
  and and_5 (and_5_out, Select, nor_1_out);
  or or_2 (or_2_out, and_2_out, and_3_out);
  or or_3 (or_3_out, and_4_out, and_5_out);
  not not_3 (not_3_out, Select_2);
  and and_6 (and_6_out, or_2_out, not_3_out);
  and and_7 (and_7_out, Select_2, or_3_out);
  or or_4 (S, and_6_out, and_7_out);

  // Notes on the sheet:
  //   Turno: tarde
  //   Mat: 651230
  //   Arquitetura de Computadores 1
  //   Pedro Herique Lima Carvalho
  //   Exemplo_0703
endmodule
