// Logisim project Pedro_Henrique_Lima_Carvalho_651230_Exemplo_0705.circ as structural Verilog: 4 circuits, main circuit main
module main (
  input  A,
  input  B,
  input  [2:0] Seletor,
  output out_4
);

  wire _000_out, _001_out, _010_out, _011_out, _100_out, _101_out, _110_out, _111_out;

  not _000 (_000_out, A);
  not _001 (_001_out, B);
  or _010 (_010_out, A, B);
  nor _011 (_011_out, A, B);
  and _100 (_100_out, A, B);
  nand _101 (_101_out, A, B);
  xor _110 (_110_out, A, B);
  xnor _111 (_111_out, A, B);
  mux8x1 mux8x1_1 (
    ._000(_000_out), ._001(_001_out), ._010(_010_out), ._011(_011_out), ._100(_100_out), ._101(_101_out),
    ._110(_110_out), ._111(_111_out), .Seletor(Seletor), .S(out_4));

  // Notes on the sheet:
  //   Turno: tarde
  //   Mat: 651230
  //   Arquitetura de Computadores 1
  //   Pedro Herique Lima Carvalho
  //   Exemplo_0705
endmodule

module mux (
  input  Select,
  input  in_0,
  input  in_1,
  output S
);

  wire and_1_out, and_2_out, not_1_out;

  not not_1 (not_1_out, Select);
  and and_1 (and_1_out, in_0, not_1_out);
  and and_2 (and_2_out, Select, in_1);
  or or_1 (S, and_1_out, and_2_out);
endmodule

module mux4x1 (
  input  [1:0] Seletor,
  input  _00,
  input  _01,
  input  _10,
  input  _11,
  output S
);

  wire mux_1_s, mux_2_s;

  mux mux_1 (.in_0(_00), .in_1(_01), .Select(Seletor[0]), .S(mux_1_s));
  mux mux_2 (.in_0(_10), .in_1(_11), .Select(Seletor[0]), .S(mux_2_s));
  mux mux_3 (.in_0(mux_1_s), .in_1(mux_2_s), .Select(Seletor[1]), .S(S));
endmodule

module mux8x1 (
  input  [2:0] Seletor,
  input  _000,
  input  _001,
  input  _010,
  input  _011,
  input  _100,
  input  _101,
  input  _110,
  input  _111,
  output S
);

  wire mux4x1_1_s, mux4x1_2_s;

  mux4x1 mux4x1_1 (._00(_000), ._01(_001), ._10(_010), ._11(_011), .Seletor(Seletor[1:0]), .S(mux4x1_1_s));
  mux4x1 mux4x1_2 (._00(_100), ._01(_101), ._10(_110), ._11(_111), .Seletor(Seletor[1:0]), .S(mux4x1_2_s));
  mux mux_1 (.in_0(mux4x1_1_s), .in_1(mux4x1_2_s), .Select(Seletor[2]), .S(S));
endmodule
