// Logisim project Pedro_Henrique_Lima_Carvalho_651230_Exemplo_0706.circ as structural Verilog: 4 circuits, main circuit mux
module main (
  input  [1:0] A,
  input  [1:0] B,
  input  Seletor,
  output out_4
);

  wire diferentes_1_s, iguais_1_s;

  Iguais iguais_1 (.A(A), .B(B), .S(iguais_1_s));
  Diferentes diferentes_1 (.A(A), .B(B), .S(diferentes_1_s));
  mux mux_1 (.in_0(iguais_1_s), .in_1(diferentes_1_s), .Select(Seletor), .S(out_4));

  // Notes on the sheet:
  //   Turno: tarde
  //   Mat: 651230
  //   Arquitetura de Computadores 1
  //   Pedro Herique Lima Carvalho
  //   Exemplo_0706
endmodule

module mux (
  input  Select,
  input  in_0,
  input  in_1,
  output S
);

  wire and_1_out, and_2_out, not_1_out;

  not not_1 (not_1_out, Select);
  and and_1 (and_1_out, in_0, not_1_out);
  and and_2 (and_2_out, Select, in_1);
  or or_1 (S, and_1_out, and_2_out);
endmodule

module Iguais (
  input  [1:0] A,
  input  [1:0] B,
  output S
);

  wire xnor_1_out, xnor_2_out;

  xnor xnor_1 (xnor_1_out, A[0], B[0]);
  and and_1 (S, xnor_1_out, xnor_2_out);
  xnor xnor_2 (xnor_2_out, A[1], B[1]);
endmodule

module Diferentes (
  input  [1:0] A,
  input  [1:0] B,
  output S
);

  wire xor_1_out, xor_2_out;

  xor xor_1 (xor_1_out, A[0], B[0]);
  xor xor_2 (xor_2_out, A[1], B[1]);
  or or_1 (S, xor_1_out, xor_2_out);
endmodule
