// Logisim project Pedro_Henrique_Lima_Carvalho_651230_Exemplo_0707.circ as structural Verilog: 4 circuits, main circuit mux
module main (
  input  [1:0] A,
  input  [1:0] B,
  input  Seletor,
  output out_4
);

  wire A_B__0_s, A_B__1_s;

  A_menor_B A_B__0 (.A(A), .B(B), .S(A_B__0_s));
  A_maior_B A_B__1 (.A(A), .B(B), .S(A_B__1_s));
  mux mux_1 (.in_0(A_B__0_s), .in_1(A_B__1_s), .Select(Seletor), .S(out_4));

  // Notes on the sheet:
  //   Turno: tarde
  //   Mat: 651230
  //   Arquitetura de Computadores 1
  //   Pedro Herique Lima Carvalho
  //   Exemplo_0707
endmodule

module mux (
  input  Select,
  input  in_0,
  input  in_1,
  output S
);

  wire and_1_out, and_2_out, not_1_out;

  not not_1 (not_1_out, Select);
  and and_1 (and_1_out, in_0, not_1_out);
  and and_2 (and_2_out, Select, in_1);
  or or_1 (S, and_1_out, and_2_out);
endmodule

module A_menor_B (
  input  [1:0] A,
  input  [1:0] B,
  output S
);

  wire and_1_out, and_2_out, and_3_out, not_1_out, not_2_out, not_3_out, not_4_out;

  not not_1 (not_1_out, A[1]);
  and and_1 (and_1_out, not_1_out, B[1]);
  not not_2 (not_2_out, A[1]);
  and and_2 (and_2_out, not_2_out, not_3_out, B[0]);
  not not_3 (not_3_out, A[0]);
  not not_4 (not_4_out, A[0]);
  and and_3 (and_3_out, not_4_out, B[1], B[0]);
  or or_1 (S, and_1_out, and_2_out, and_3_out);
endmodule

module A_maior_B (
  input  [1:0] A,
  input  [1:0] B,
  output S
);

  wire and_1_out, and_2_out, and_3_out, not_1_out, not_2_out, not_3_out, not_4_out;

  and and_1 (and_1_out, A[1], not_1_out);
  not not_1 (not_1_out, B[1]);
  not not_2 (not_2_out, B[1]);
  and and_2 (and_2_out, A[0], not_2_out, not_3_out);
  not not_3 (not_3_out, B[0]);
  and and_3 (and_3_out, A[1], A[0], not_4_out);
  not not_4 (not_4_out, B[0]);
  or or_1 (S, and_1_out, and_2_out, and_3_out);
endmodule
