// Logisim project Pedro_Henrique_Lima_Carvalho_651230_Exemplo_0802.circ as structural Verilog: 4 circuits, main circuit main
module main (
  input  [3:0] A,
  input  [3:0] B,
  output [3:0] A_B,
  output Borrows
);

  wire full_subt_1_borrows, full_subt_2_half_1_borrows, full_subt_2_half_2_borrows;

  Full_Subt full_subt_1 (.A(A[0]), .B(B[0]), .Borrowed(1'b0), .Borrows(full_subt_1_borrows), .S(A_B[0]));
  Full_Subt__2_Half full_subt_2_half_1 (
    .A(A[1]), .B(B[1]), .Borrowed(full_subt_1_borrows), .Borrows(full_subt_2_half_1_borrows), .S(A_B[1]));
  Full_Subt__2_Half full_subt_2_half_2 (
    .A(A[2]), .B(B[2]), .Borrowed(full_subt_2_half_1_borrows), .Borrows(full_subt_2_half_2_borrows),
    .S(A_B[2]));
  Full_Subt__2_Half full_subt_2_half_3 (
    .A(A[3]), .B(B[3]), .Borrowed(full_subt_2_half_2_borrows), .Borrows(Borrows), .S(A_B[3]));

  // Notes on the sheet:
  //   Turno: tarde
  //   Mat: 651230
  //   Exemplo_0802
  //   Arquitetura de Computadores 1
  //   Pedro Herique Lima Carvalho
endmodule

module Half_Subt (
  input  A,
  input  B,
  output S0,
  output Borrow_In
);

  wire not_1_out;

  not not_1 (not_1_out, A);
  xor xor_1 (S0, A, B);
  and and_1 (Borrow_In, not_1_out, B);

  // Notes on the sheet:
  //   Half Subtractor
endmodule

module Full_Subt (
  input  A,
  input  B,
  input  Borrowed,
  output S,
  output Borrows
);

  wire and_1_out, and_2_out, and_3_out, and_4_out, and_5_out, not_1_out, xnor_1_out, xor_1_out;

  not not_1 (not_1_out, A);
  xor xor_1 (xor_1_out, B, Borrowed);
  xnor xnor_1 (xnor_1_out, B, Borrowed);
  and and_1 (and_1_out, not_1_out, B);
  and and_2 (and_2_out, B, Borrowed);
  and and_3 (and_3_out, not_1_out, Borrowed);
  and and_4 (and_4_out, xor_1_out, not_1_out);
  and and_5 (and_5_out, A, xnor_1_out);
  or or_1 (Borrows, and_1_out, and_2_out, and_3_out);
  or or_2 (S, and_4_out, and_5_out);

  // Notes on the sheet:
  //   Full Subtractor
endmodule

module Full_Subt__2_Half (
  input  A,
  input  B,
  input  Borrowed,
  output S,
  output Borrows
);

  wire half_subt_1_borrow_in, half_subt_1_s0, half_subt_2_borrow_in;

  Half_Subt half_subt_1 (.A(A), .B(B), .Borrow_In(half_subt_1_borrow_in), .S0(half_subt_1_s0));
  Half_Subt half_subt_2 (.A(half_subt_1_s0), .B(Borrowed), .Borrow_In(half_subt_2_borrow_in), .S0(S));
  or or_1 (Borrows, half_subt_2_borrow_in, half_subt_1_borrow_in);

  // Notes on the sheet:
  //   Full Adder
endmodule
