// Logisim project Pedro_Henrique_Lima_Carvalho_651230_Exemplo_0803.circ as structural Verilog: 1 circuit, main circuit main
module main (
  input  [3:0] A,
  input  [3:0] B,
  output [3:0] Bitwise,
  output Logical
);

  xnor xnor_1 (Bitwise[0], A[0], B[0]);
  xnor xnor_2 (Bitwise[1], A[1], B[1]);
  xnor xnor_3 (Bitwise[2], A[2], B[2]);
  xnor xnor_4 (Bitwise[3], A[3], B[3]);
  and and_1 (Logical, Bitwise[3], Bitwise[2], Bitwise[1], Bitwise[0]);

  // Notes on the sheet:
  //   Turno: tarde
  //   Mat: 651230
  //   Exemplo_0803
  //   Arquitetura de Computadores 1
  //   Pedro Herique Lima Carvalho
endmodule
