// Logisim project Pedro_Henrique_Lima_Carvalho_651230_Exemplo_0804.circ as structural Verilog: 1 circuit, main circuit main
module main (
  input  [3:0] A,
  input  [3:0] B,
  output [3:0] Bitwise,
  output Logical
);

  xor xor_1 (Bitwise[0], A[0], B[0]);
  xor xor_2 (Bitwise[1], A[1], B[1]);
  xor xor_3 (Bitwise[2], A[2], B[2]);
  xor xor_4 (Bitwise[3], A[3], B[3]);
  or or_1 (Logical, Bitwise[3], Bitwise[2], Bitwise[1], Bitwise[0]);

  // Notes on the sheet:
  //   Turno: tarde
  //   Mat: 651230
  //   Exemplo_0804
  //   Arquitetura de Computadores 1
  //   Pedro Herique Lima Carvalho
endmodule
