// Logisim project Pedro_Henrique_Lima_Carvalho_651230_Exemplo_0805.circ as structural Verilog: 4 circuits, main circuit main
module main (
  input  [3:0] A,
  output [3:0] minus_A
);

  wire full_adder_1_carry_out, full_adder_2_carry_out, full_adder_2_half_1_carry_out, full_adder_3_carry_out;
  wire [3:0] not_1_out;

  assign not_1_out = ~A;  // NOT_Gate not_1, 4 bits wide
  Full_Adder__2_Half full_adder_2_half_1 (
    .A(not_1_out[0]), .B(1'b0), .Carry_In(1'b1), .Carry_Out(full_adder_2_half_1_carry_out), .S(minus_A[0]));
  Full_Adder full_adder_1 (
    .A(not_1_out[1]), .B(1'b0), .Carry_In(full_adder_2_half_1_carry_out), .Carry_Out(full_adder_1_carry_out),
    .S(minus_A[1]));
  Full_Adder full_adder_2 (
    .A(not_1_out[2]), .B(1'b0), .Carry_In(full_adder_1_carry_out), .Carry_Out(full_adder_2_carry_out),
    .S(minus_A[2]));
  Full_Adder full_adder_3 (
    .A(not_1_out[3]), .B(1'b0), .Carry_In(full_adder_2_carry_out), .Carry_Out(full_adder_3_carry_out),
    .S(minus_A[3]));
  // also tied to GND on the sheet: full_adder_3_carry_out

  // Notes on the sheet:
  //   Turno: tarde
  //   Mat: 651230
  //   Exemplo_0805
  //   Arquitetura de Computadores 1
  //   Pedro Herique Lima Carvalho
endmodule

module HalfAdder (
  input  A,
  input  B,
  output S0,
  output Carry_Out
);

  xor xor_1 (S0, A, B);
  and and_1 (Carry_Out, A, B);

  // Notes on the sheet:
  //   Half Adder
endmodule

module Full_Adder (
  input  A,
  input  B,
  input  Carry_In,
  output S,
  output Carry_Out
);

  wire and_1_out, and_2_out, and_3_out, and_4_out, and_5_out, not_1_out, xnor_1_out, xor_1_out;

  not not_1 (not_1_out, A);
  xor xor_1 (xor_1_out, B, Carry_In);
  xnor xnor_1 (xnor_1_out, B, Carry_In);
  and and_1 (and_1_out, A, B);
  and and_2 (and_2_out, B, Carry_In);
  and and_3 (and_3_out, A, Carry_In);
  and and_4 (and_4_out, xor_1_out, not_1_out);
  and and_5 (and_5_out, A, xnor_1_out);
  or or_1 (Carry_Out, and_1_out, and_2_out, and_3_out);
  or or_2 (S, and_4_out, and_5_out);

  // Notes on the sheet:
  //   Full Adder
endmodule

module Full_Adder__2_Half (
  input  A,
  input  B,
  input  Carry_In,
  output S,
  output Carry_Out
);

  wire halfadder_1_carry_out, halfadder_1_s0, halfadder_2_carry_out;

  HalfAdder halfadder_1 (.A(B), .B(A), .Carry_Out(halfadder_1_carry_out), .S0(halfadder_1_s0));
  HalfAdder halfadder_2 (.A(Carry_In), .B(halfadder_1_s0), .Carry_Out(halfadder_2_carry_out), .S0(S));
  or or_1 (Carry_Out, halfadder_2_carry_out, halfadder_1_carry_out);

  // Notes on the sheet:
  //   Full Adder
endmodule
