// Logisim project Pedro_Henrique_Lima_Carvalho_651230_Exemplo_0806.circ as structural Verilog: 5 circuits, main circuit main
module main (
  input  [3:0] A,
  input  [3:0] B,
  input  Seletor,
  input  AU_LU,
  output [3:0] S,
  output Carry_Out
);

  wire full_adder_1_carry_out, full_adder_2_carry_out, full_adder_2_half_1_carry_out;
  wire [3:0] full_adder_2_half_1_s, xor_1_out;
  wire [3:3] or_1_out;

  assign xor_1_out = B ^ {4{or_1_out[3]}};  // XOR_Gate xor_1, 4 bits wide
  or or_1 (or_1_out[3], Seletor, AU_LU);
  Full_Adder__2_Half full_adder_2_half_1 (
    .A(A[0]), .B(xor_1_out[0]), .Carry_In(or_1_out[3]), .Carry_Out(full_adder_2_half_1_carry_out),
    .S(full_adder_2_half_1_s[0]));
  Full_Adder full_adder_1 (
    .A(A[1]), .B(xor_1_out[1]), .Carry_In(full_adder_2_half_1_carry_out), .Carry_Out(full_adder_1_carry_out),
    .S(full_adder_2_half_1_s[1]));
  Full_Adder full_adder_2 (
    .A(A[2]), .B(xor_1_out[2]), .Carry_In(full_adder_1_carry_out), .Carry_Out(full_adder_2_carry_out),
    .S(full_adder_2_half_1_s[2]));
  Full_Adder full_adder_3 (
    .A(A[3]), .B(xor_1_out[3]), .Carry_In(full_adder_2_carry_out), .Carry_Out(Carry_Out),
    .S(full_adder_2_half_1_s[3]));
  LU lu_1 (.In(full_adder_2_half_1_s), .AU_LU(AU_LU), .Out(S));

  // Notes on the sheet:
  //   Turno: tarde
  //   Mat: 651230
  //   Exemplo_0806
  //   Arquitetura de Computadores 1
  //   Pedro Herique Lima Carvalho
endmodule

module HalfAdder (
  input  A,
  input  B,
  output S0,
  output Carry_Out
);

  xor xor_1 (S0, A, B);
  and and_1 (Carry_Out, A, B);

  // Notes on the sheet:
  //   Half Adder
endmodule

// FA
module Full_Adder (
  input  A,
  input  B,
  input  Carry_In,
  output S,
  output Carry_Out
);

  wire and_1_out, and_2_out, and_3_out, and_4_out, and_5_out, not_1_out, xnor_1_out, xor_1_out;

  not not_1 (not_1_out, A);
  xor xor_1 (xor_1_out, B, Carry_In);
  xnor xnor_1 (xnor_1_out, B, Carry_In);
  and and_1 (and_1_out, A, B);
  and and_2 (and_2_out, B, Carry_In);
  and and_3 (and_3_out, A, Carry_In);
  and and_4 (and_4_out, xor_1_out, not_1_out);
  and and_5 (and_5_out, A, xnor_1_out);
  or or_1 (Carry_Out, and_1_out, and_2_out, and_3_out);
  or or_2 (S, and_4_out, and_5_out);

  // Notes on the sheet:
  //   Full Adder
endmodule

// FA
module Full_Adder__2_Half (
  input  A,
  input  B,
  input  Carry_In,
  output S,
  output Carry_Out
);

  wire halfadder_1_carry_out, halfadder_1_s0, halfadder_2_carry_out;

  HalfAdder halfadder_1 (.A(B), .B(A), .Carry_Out(halfadder_1_carry_out), .S0(halfadder_1_s0));
  HalfAdder halfadder_2 (.A(Carry_In), .B(halfadder_1_s0), .Carry_Out(halfadder_2_carry_out), .S0(S));
  or or_1 (Carry_Out, halfadder_2_carry_out, halfadder_1_carry_out);

  // Notes on the sheet:
  //   Full Adder
endmodule

module LU (
  input  AU_LU,
  input  [3:0] In,
  output [3:0] Out
);

  wire [0:0] nor_1_out;

  nor nor_1 (nor_1_out[0], In[0], In[1], In[2], In[3]);
  Multiplexer #(.width(4), .enable("false")) multiplexer_1 (
    .in0(In), .in1({3'b000, nor_1_out[0]}), .out(Out), .sel(AU_LU));
endmodule
