// Logisim project Pedro_Henrique_Lima_Carvalho_651230_Exemplo_0807.circ as structural Verilog: 5 circuits, main circuit main
module main (
  input  Selector,
  input  [3:0] A,
  input  [3:0] B,
  output [3:0] Bitwise,
  output Logical
);

  wire equals_1_logical, not_equals_1_logical;
  wire [3:0] equals_1_bitwise, not_equals_1_bitwise;

  equals equals_1 (.A(A), .B(B), .Bitwise(equals_1_bitwise), .Logical(equals_1_logical));
  not_equals not_equals_1 (.A(A), .B(B), .Bitwise(not_equals_1_bitwise), .Logical(not_equals_1_logical));
  mux4_b mux4_b_1 (.A(equals_1_bitwise), .B(not_equals_1_bitwise), .Select(Selector), .S(Bitwise));
  mux1_b mux1_b_1 (.A(equals_1_logical), .B(not_equals_1_logical), .Selector(Selector), .S(Logical));

  // Notes on the sheet:
  //   Turno: tarde
  //   Mat: 651230
  //   Arquitetura de Computadores 1
  //   Pedro Herique Lima Carvalho
  //   Exemplo_0807
endmodule

// Eq
module equals (
  input  [3:0] A,
  input  [3:0] B,
  output [3:0] Bitwise,
  output Logical
);

  xnor xnor_1 (Bitwise[0], A[0], B[0]);
  xnor xnor_2 (Bitwise[1], A[1], B[1]);
  xnor xnor_3 (Bitwise[2], A[2], B[2]);
  xnor xnor_4 (Bitwise[3], A[3], B[3]);
  and and_1 (Logical, Bitwise[3], Bitwise[2], Bitwise[1], Bitwise[0]);
endmodule

// !Eq
module not_equals (
  input  [3:0] A,
  input  [3:0] B,
  output [3:0] Bitwise,
  output Logical
);

  xor xor_1 (Bitwise[0], A[0], B[0]);
  xor xor_2 (Bitwise[1], A[1], B[1]);
  xor xor_3 (Bitwise[2], A[2], B[2]);
  xor xor_4 (Bitwise[3], A[3], B[3]);
  or or_1 (Logical, Bitwise[3], Bitwise[2], Bitwise[1], Bitwise[0]);
endmodule

// M4'b
module mux4_b (
  input  Select,
  input  [3:0] A,
  input  [3:0] B,
  output [3:0] S
);

  wire [3:0] and_1_out, and_2_out, not_1_out;

  assign not_1_out = ~{4{Select}};  // NOT_Gate not_1, 4 bits wide
  assign and_1_out = not_1_out & A;  // AND_Gate and_1, 4 bits wide
  assign S = and_1_out | and_2_out;  // OR_Gate or_1, 4 bits wide
  assign and_2_out = {4{Select}} & B;  // AND_Gate and_2, 4 bits wide
endmodule

// M1'b
module mux1_b (
  input  Selector,
  input  A,
  input  B,
  output S
);

  wire and_1_out, and_2_out, not_1_out;

  not not_1 (not_1_out, Selector);
  and and_1 (and_1_out, not_1_out, A);
  and and_2 (and_2_out, Selector, B);
  or or_1 (S, and_1_out, and_2_out);
endmodule
