// Logisim project Pedro_Henrique_Lima_Carvalho_651230_Exemplo_07.circ as structural Verilog: 1 circuit, main circuit main
module main (
  input  All_1,
  input  Load,
  input  All_0,
  output Result
);

  wire clock_1_out, not_1_out, not_2_out, not_3_out, not_4_out, not_5_out, s_r_ff_1_q, s_r_ff_2_q, s_r_ff_3_q;

  Clock clock_1 (.out(clock_1_out));
  not not_1 (not_1_out, Load);
  S_R_Flip_Flop s_r_ff_1 (
    .S(Load), .clk(clock_1_out), .R(not_1_out), .Q(s_r_ff_1_q), .preset(All_1), .reset(All_0));  // open: Qn
  not not_2 (not_2_out, s_r_ff_1_q);
  and and_1 (Result, not_3_out, s_r_ff_2_q, not_4_out);
  not not_3 (not_3_out, s_r_ff_1_q);
  not not_4 (not_4_out, s_r_ff_3_q);
  S_R_Flip_Flop s_r_ff_2 (
    .S(s_r_ff_1_q), .clk(clock_1_out), .R(not_2_out), .Q(s_r_ff_2_q), .preset(All_1), .reset(All_0));  // open: Qn
  not not_5 (not_5_out, s_r_ff_2_q);
  S_R_Flip_Flop s_r_ff_3 (
    .S(s_r_ff_2_q), .clk(clock_1_out), .R(not_5_out), .Q(s_r_ff_3_q), .preset(All_1), .reset(All_0));  // open: Qn

  // Notes on the sheet:
  //   Mat: 651230
  //   Exemplo 07
  //   Pedro Henrique Lima Carvalho
endmodule
