// Logisim project Mealy_1101.circ as structural Verilog: 1 circuit, main circuit main
module main (
  input  Pulse,
  input  Clear,
  output Detected
);

  wire clock_1_out, d_ff_1_q, d_ff_2_q, d_ff_2_qn, d_ff_3_q, d_ff_4_q;

  Clock clock_1 (.out(clock_1_out));
  D_Flip_Flop d_ff_1 (.clk(clock_1_out), .D(Pulse), .Q(d_ff_1_q), .reset(Clear));  // open: Qn, preset
  D_Flip_Flop d_ff_2 (.clk(clock_1_out), .D(d_ff_1_q), .Q(d_ff_2_q), .Qn(d_ff_2_qn), .reset(Clear));  // open: preset
  and and_1 (Detected, d_ff_4_q, d_ff_3_q, d_ff_2_qn, d_ff_1_q);
  D_Flip_Flop d_ff_3 (.clk(clock_1_out), .D(d_ff_2_q), .Q(d_ff_3_q), .reset(Clear));  // open: Qn, preset
  D_Flip_Flop d_ff_4 (.clk(clock_1_out), .D(d_ff_3_q), .Q(d_ff_4_q), .reset(Clear));  // open: Qn, preset

  // Notes on the sheet:
  //   Mat: 651230
  //   Arquitetura de Computadores 1
  //   Pedro Henrique Lima Carvalho
endmodule
