// Logisim project Pedro_Henrique_Lima_Carvalho_651230_Exemplo_1101.circ as structural Verilog: 3 circuits, main circuit main
module main (
  input  clear,
  output Detected,
  output Detected_2
);

  wire clk, shift_register_1_out;

  Clock clock_1 (.out(clk));
  Shift_Register #(.length(4)) shift_register_1 (
    .clk(clk), .out(shift_register_1_out), .clr(clear));  // open: shift, in, load, d0, q0, d1, q1, d2, q2, d3, q3
  mealy Mealy (.Clock(clk), .Pulse(shift_register_1_out), .Clear(clear), .Detected(Detected));
  moore Moore (.Clock(clk), .Pulse(shift_register_1_out), .Clear(clear), .Detected(Detected_2));

  // Notes on the sheet:
  //   Mat: 651230
  //   Arquitetura de Computadores 1
  //   Pedro Henrique Lima Carvalho
  //   Manual 
  //   Insertion
endmodule

module mealy (
  input  Clock,
  input  Pulse,
  input  Clear,
  output Detected
);

  wire d_ff_1_q, d_ff_2_q, d_ff_2_qn, d_ff_3_q, d_ff_4_q;

  D_Flip_Flop d_ff_1 (.clk(Clock), .D(Pulse), .Q(d_ff_1_q), .reset(Clear));  // open: Qn, preset
  D_Flip_Flop d_ff_2 (.clk(Clock), .D(d_ff_1_q), .Q(d_ff_2_q), .Qn(d_ff_2_qn), .reset(Clear));  // open: preset
  and and_1 (Detected, d_ff_4_q, d_ff_3_q, d_ff_2_qn, d_ff_1_q);
  D_Flip_Flop d_ff_3 (.clk(Clock), .D(d_ff_2_q), .Q(d_ff_3_q), .reset(Clear));  // open: Qn, preset
  D_Flip_Flop d_ff_4 (.clk(Clock), .D(d_ff_3_q), .Q(d_ff_4_q), .reset(Clear));  // open: Qn, preset

  // Notes on the sheet:
  //   Mat: 651230
  //   Arquitetura de Computadores 1
  //   Pedro Henrique Lima Carvalho
endmodule

module moore (
  input  Clock,
  input  Pulse,
  input  Clear,
  output Detected
);

  wire and_1_out, d_ff_1_q, d_ff_2_q, d_ff_2_qn, d_ff_3_q, d_ff_5_q;

  D_Flip_Flop d_ff_1 (.clk(Clock), .D(Pulse), .Q(d_ff_1_q), .reset(Clear));  // open: Qn, preset
  D_Flip_Flop d_ff_2 (.clk(Clock), .D(d_ff_1_q), .Q(d_ff_2_q), .Qn(d_ff_2_qn), .reset(Clear));  // open: preset
  and and_1 (and_1_out, d_ff_5_q, d_ff_3_q, d_ff_2_qn, d_ff_1_q);
  D_Flip_Flop d_ff_3 (.clk(Clock), .D(d_ff_2_q), .Q(d_ff_3_q), .reset(Clear));  // open: Qn, preset
  D_Flip_Flop #(.trigger("falling")) d_ff_4 (
    .clk(Clock), .D(and_1_out), .Q(Detected), .reset(Clear));  // open: Qn, preset
  D_Flip_Flop d_ff_5 (.clk(Clock), .D(d_ff_3_q), .Q(d_ff_5_q), .reset(Clear));  // open: Qn, preset

  // Notes on the sheet:
  //   Mat: 651230
  //   Arquitetura de Computadores 1
  //   Pedro Henrique Lima Carvalho
endmodule
