// Logisim project Pedro_Henrique_Lima_Carvalho_651230_Exemplo_1103.circ as structural Verilog: 2 circuits, main circuit main
module main (
  input  clear,
  output Detected
);

  wire clk, shift_register_1_p3, shift_register_1_p5;

  Clock clock_1 (.out(clk));
  // Shift_Register #(.length(9)) shift_register_1: pin names not known; wires that end beside it: clk, clear, shift_register_1_p3, shift_register_1_p3, shift_register_1_p5
  moore Moore (.Clock(clk), .Pulse(shift_register_1_p5), .Clear(clear), .Detected(Detected));

  // Notes on the sheet:
  //   Mat: 651230
  //   Arquitetura de Computadores 1
  //   Pedro Henrique Lima Carvalho
  //   Manual 
  //   Insertion
endmodule

module moore (
  input  Clock,
  input  Pulse,
  input  Clear,
  output Detected
);

  wire and_1_out, d_ff_1_q, d_ff_1_qn, d_ff_2_q, d_ff_3_q, d_ff_3_qn, d_ff_5_q;

  D_Flip_Flop d_ff_1 (.clk(Clock), .D(Pulse), .Q(d_ff_1_q), .Qn(d_ff_1_qn), .reset(Clear));  // open: preset
  D_Flip_Flop d_ff_2 (.clk(Clock), .D(d_ff_1_q), .Q(d_ff_2_q), .reset(Clear));  // open: Qn, preset
  and and_1 (and_1_out, d_ff_5_q, d_ff_3_qn, d_ff_2_q, d_ff_1_qn);
  D_Flip_Flop d_ff_3 (.clk(Clock), .D(d_ff_2_q), .Q(d_ff_3_q), .Qn(d_ff_3_qn), .reset(Clear));  // open: preset
  D_Flip_Flop #(.trigger("falling")) d_ff_4 (
    .clk(Clock), .D(and_1_out), .Q(Detected), .reset(Clear));  // open: Qn, preset
  D_Flip_Flop d_ff_5 (.clk(Clock), .D(d_ff_3_q), .Q(d_ff_5_q), .reset(Clear));  // open: Qn, preset

  // Notes on the sheet:
  //   Mat: 651230
  //   Arquitetura de Computadores 1
  //   Pedro Henrique Lima Carvalho
endmodule
