// Logisim project Pedro_Henrique_Lima_Carvalho_651230_Exemplo_1104.circ as structural Verilog: 2 circuits, main circuit main
module main (
  input  clear,
  output Detected
);

  wire clk, shift_register_1_p3, shift_register_1_p5;

  Clock clock_1 (.out(clk));
  // Shift_Register #(.length(9)) shift_register_1: pin names not known; wires that end beside it: clk, clear, shift_register_1_p3, shift_register_1_p3, shift_register_1_p5
  FSM fsm_1 (.Clock(clk), .Pulse(shift_register_1_p5), .Clear(clear), .Detected(Detected));

  // Notes on the sheet:
  //   Mat: 651230
  //   Arquitetura de Computadores 1
  //   Pedro Henrique Lima Carvalho
  //   Manual 
  //   Insertion
endmodule

module FSM (
  input  Clock,
  input  Pulse,
  input  Clear,
  output Detected
);

  wire and_1_out, controlled_buffer_1_out, d_ff_1_q, d_ff_2_q, d_ff_2_qn, d_ff_3_q, d_ff_5_q, or_1_out;

  or or_1 (or_1_out, controlled_buffer_1_out, Clear);
  D_Flip_Flop d_ff_1 (.clk(Clock), .D(Pulse), .Q(d_ff_1_q), .reset(or_1_out));  // open: Qn, preset
  D_Flip_Flop d_ff_2 (.clk(Clock), .D(d_ff_1_q), .Q(d_ff_2_q), .Qn(d_ff_2_qn), .reset(or_1_out));  // open: preset
  and and_1 (and_1_out, d_ff_3_q, d_ff_2_qn, d_ff_1_q);
  D_Flip_Flop d_ff_3 (.clk(Clock), .D(d_ff_2_q), .Q(d_ff_3_q), .reset(or_1_out));  // open: Qn, preset
  D_Flip_Flop #(.trigger("falling")) d_ff_4 (
    .clk(Clock), .D(and_1_out), .Q(Detected), .reset(or_1_out));  // open: Qn, preset
  assign controlled_buffer_1_out = ~Detected ? d_ff_5_q : 1'bz;  // Controlled_Buffer controlled_buffer_1
  D_Flip_Flop d_ff_5 (.clk(Detected), .D(Detected), .Q(d_ff_5_q), .reset(Clear));  // open: Qn, preset

  // Notes on the sheet:
  //   Mat: 651230
  //   Arquitetura de Computadores 1
  //   Pedro Henrique Lima Carvalho
endmodule
