// Logisim project Pedro_Henrique_Lima_Carvalho_651230_Exemplo_1106.circ as structural Verilog: 2 circuits, main circuit main
module main (
  input  clear,
  output Detected
);

  wire clk, shift_register_1_out;

  Clock clock_1 (.out(clk));
  Shift_Register #(.length(3)) shift_register_1 (
    .clk(clk), .out(shift_register_1_out), .clr(clear));  // open: shift, in, load, d0, q0, d1, q1, d2, q2
  FSM fsm_1 (.Clock(clk), .Pulse(shift_register_1_out), .Clear(clear), .Detected(Detected));

  // Notes on the sheet:
  //   Mat: 651230
  //   Arquitetura de Computadores 1
  //   Pedro Henrique Lima Carvalho
  //   Manual 
  //   Insertion
endmodule

module FSM (
  input  Clock,
  input  Pulse,
  input  Clear,
  output Detected
);

  wire and_2_out, Bit_3_Ctl, d_ff_1_q, d_ff_2_q, d_ff_3_q, nor_1_out, not_1_out, or_1_out;
  wire [1:0] counter_1_q;

  Counter #(.width(2), .max('h3), .ongoal("stay")) counter_1 (
    .D({1'b0, Clock}), .Q(counter_1_q), .clk(Clock), .clr(Clear));  // open: load, count, carry, preset, down
  D_Flip_Flop d_ff_1 (.clk(Clock), .D(Pulse), .Q(d_ff_1_q), .reset(Clear));  // open: Qn, preset
  and and_1 (Bit_3_Ctl, counter_1_q[0], counter_1_q[1]);
  D_Flip_Flop d_ff_2 (.clk(Clock), .D(d_ff_1_q), .Q(d_ff_2_q), .reset(Clear));  // open: Qn, preset
  D_Flip_Flop d_ff_3 (.clk(Clock), .D(d_ff_2_q), .Q(d_ff_3_q), .reset(Clear));  // open: Qn, preset
  nor nor_1 (nor_1_out, d_ff_2_q, d_ff_2_q, d_ff_3_q, not_1_out);
  not not_1 (not_1_out, Bit_3_Ctl);
  and and_2 (and_2_out, Bit_3_Ctl, d_ff_3_q, d_ff_2_q, d_ff_1_q);
  or or_1 (or_1_out, nor_1_out, and_2_out);
  D_Flip_Flop #(.trigger("falling")) d_ff_4 (
    .clk(Clock), .D(or_1_out), .Q(Detected), .reset(Clear));  // open: Qn, preset

  // Notes on the sheet:
  //   Mat: 651230
  //   Arquitetura de Computadores 1
  //   Pedro Henrique Lima Carvalho
endmodule
