// Logisim project Pedro_Henrique_Lima_Carvalho_651230_Exemplo_Exemplo_1201.circ as structural Verilog: 3 circuits, main circuit main
module main (
  input  Addr,
  input  R_W,
  input  [3:0] In,
  input  Clear,
  output [3:0] Out
);

  wire clock_1_out;

  Clock clock_1 (.out(clock_1_out));
  Ram_1x4 ram_1x4_1 (.Addr(Addr), .R_W(R_W), .Clk(clock_1_out), .In(In), .Clear(Clear), .Out(Out));

  // Notes on the sheet:
  //   Mat: 651230
  //   Arquitetura de Computadores I
  //   Pedro Henrique Lima Carvalho
endmodule

module Ram_1x1 (
  input  Addr,
  input  R_W,
  input  Clk,
  input  In,
  input  Clear,
  output Out
);

  wire and_1_out, j_k_ff_1_q, not_1_out;

  and and_1 (and_1_out, Addr, R_W, Clk);
  not not_1 (not_1_out, In);
  J_K_Flip_Flop j_k_ff_1 (.J(In), .clk(and_1_out), .K(not_1_out), .Q(j_k_ff_1_q), .reset(Clear));  // open: Qn, preset
  and and_2 (Out, Addr, j_k_ff_1_q);

  // Notes on the sheet:
  //   Mat: 651230
  //   Arquitetura de Computadores I
  //   Pedro Henrique Lima Carvalho
endmodule

module Ram_1x4 (
  input  Addr,
  input  R_W,
  input  Clk,
  input  [3:0] In,
  input  Clear,
  output [3:0] Out
);

  wire _0, _1, _2;
  wire [3:3] ram_1x1_4_out;

  Ram_1x1 ram_1x1_1 (.Addr(Addr), .R_W(R_W), .Clk(Clk), .In(In[0]), .Clear(Clear), .Out(_0));
  Ram_1x1 ram_1x1_2 (.Addr(Addr), .R_W(R_W), .Clk(Clk), .In(In[1]), .Clear(Clear), .Out(_1));
  Ram_1x1 ram_1x1_3 (.Addr(Addr), .R_W(R_W), .Clk(Clk), .In(In[2]), .Clear(Clear), .Out(_2));
  Ram_1x1 ram_1x1_4 (.Addr(Addr), .R_W(R_W), .Clk(Clk), .In(In[3]), .Clear(Clear), .Out(ram_1x1_4_out[3]));
  assign Out = {4{Addr}} & {ram_1x1_4_out[3], _2, _1, _0};  // AND_Gate and_1, 4 bits wide

  // Notes on the sheet:
  //   Mat: 651230
  //   Arquitetura de Computadores I
  //   Pedro Henrique Lima Carvalho
endmodule
