// Logisim project Pedro_Henrique_Lima_Carvalho_651230_Exemplo_Exemplo_1203.circ as structural Verilog: 5 circuits, main circuit main
module main (
  input  Addr,
  input  R_W,
  input  [7:0] In,
  input  Clear,
  output [7:0] Out
);

  wire clock_1_out;

  Clock clock_1 (.out(clock_1_out));
  Ram_2x8 ram_2x8_1 (.Addr(Addr), .R_W(R_W), .Clk(clock_1_out), .in_4(In), .Clear(Clear), .out_6(Out));

  // Notes on the sheet:
  //   Mat: 651230
  //   Arquitetura de Computadores I
  //   Pedro Henrique Lima Carvalho
endmodule

module Ram_1x1 (
  input  Addr,
  input  R_W,
  input  Clk,
  input  In,
  input  Clear,
  output Out
);

  wire and_1_out, j_k_ff_1_q, not_1_out;

  and and_1 (and_1_out, Addr, R_W, Clk);
  not not_1 (not_1_out, In);
  J_K_Flip_Flop j_k_ff_1 (.J(In), .clk(and_1_out), .K(not_1_out), .Q(j_k_ff_1_q), .reset(Clear));  // open: Qn, preset
  and and_2 (Out, Addr, j_k_ff_1_q);

  // Notes on the sheet:
  //   Mat: 651230
  //   Arquitetura de Computadores I
  //   Pedro Henrique Lima Carvalho
endmodule

module Ram_1x2 (
  input  Addr,
  input  R_W,
  input  Clk,
  input  [1:0] In,
  input  Clear,
  output [1:0] Out
);

  wire _0, _1;

  Ram_1x1 ram_1x1_1 (.Addr(Addr), .R_W(R_W), .Clk(Clk), .In(In[0]), .Clear(Clear), .Out(_0));
  Ram_1x1 ram_1x1_2 (.Addr(Addr), .R_W(R_W), .Clk(Clk), .In(In[1]), .Clear(Clear), .Out(_1));
  assign Out = {2{Addr}} & {_1, _0};  // AND_Gate and_1, 2 bits wide

  // Notes on the sheet:
  //   Mat: 651230
  //   Arquitetura de Computadores I
  //   Pedro Henrique Lima Carvalho
endmodule

module Ram_1x4_2de1x2 (
  input  Addr,
  input  R_W,
  input  Clk,
  input  [3:0] In,
  input  Clear,
  output [3:0] Out
);

  wire [1:0] ram_1x2_1_out, ram_1x2_2_out;

  Ram_1x2 ram_1x2_1 (.Addr(Addr), .R_W(R_W), .Clk(Clk), .In(In[1:0]), .Clear(Clear), .Out(ram_1x2_1_out));
  Ram_1x2 ram_1x2_2 (.Addr(Addr), .R_W(R_W), .Clk(Clk), .In(In[3:2]), .Clear(Clear), .Out(ram_1x2_2_out));
  assign Out = {4{Addr}} & {ram_1x2_2_out, ram_1x2_1_out};  // AND_Gate and_1, 4 bits wide

  // Notes on the sheet:
  //   Mat: 651230
  //   Arquitetura de Computadores I
  //   Pedro Henrique Lima Carvalho
endmodule

module Ram_2x8 (
  input  Addr,
  input  R_W,
  input  Clk,
  input  [7:0] in_4,
  input  Clear,
  output [7:0] out_6
);

  wire not_1_out, not_2_out;
  wire [3:0] ram_1x4_2de1x2_1_out, ram_1x4_2de1x2_2_out, ram_1x4_2de1x2_3_out, ram_1x4_2de1x2_4_out;

  not not_1 (not_1_out, Addr);
  Ram_1x4_2de1x2 ram_1x4_2de1x2_1 (
    .Addr(not_1_out), .R_W(R_W), .Clk(Clk), .In(in_4[3:0]), .Clear(Clear), .Out(ram_1x4_2de1x2_1_out));
  Ram_1x4_2de1x2 ram_1x4_2de1x2_2 (
    .Addr(Addr), .R_W(R_W), .Clk(Clk), .In(in_4[3:0]), .Clear(Clear), .Out(ram_1x4_2de1x2_2_out));
  Ram_1x4_2de1x2 ram_1x4_2de1x2_3 (
    .Addr(not_1_out), .R_W(R_W), .Clk(Clk), .In(in_4[7:4]), .Clear(Clear), .Out(ram_1x4_2de1x2_3_out));
  Ram_1x4_2de1x2 ram_1x4_2de1x2_4 (
    .Addr(Addr), .R_W(R_W), .Clk(Clk), .In(in_4[7:4]), .Clear(Clear), .Out(ram_1x4_2de1x2_4_out));
  not not_2 (not_2_out, not_1_out);
  Multiplexer #(.width(8), .enable("false")) multiplexer_1 (
    .in0({ram_1x4_2de1x2_3_out, ram_1x4_2de1x2_1_out}), .in1({ram_1x4_2de1x2_4_out, ram_1x4_2de1x2_2_out}),
    .out(out_6), .sel(not_2_out));

  // Other names for the same wires on the sheet: _4_7[3:0] = in_4[7:4]

  // Notes on the sheet:
  //   Mat: 651230
  //   Arquitetura de Computadores I
  //   Pedro Henrique Lima Carvalho
endmodule
