// Logisim project Pedro_Henrique_Lima_Carvalho_651230_Exemplo_Exemplo_1205.circ as structural Verilog: 7 circuits, main circuit main
module main (
  input  [2:0] Addr,
  input  R_W,
  input  [7:0] In,
  input  Clear,
  output [7:0] Out
);

  wire clock_1_out;

  Clock clock_1 (.out(clock_1_out));
  Ram_8x8 ram_8x8_1 (.Addr(Addr), .R_W(R_W), .Clk(clock_1_out), .In(In), .Clear(Clear), .Out(Out));

  // Notes on the sheet:
  //   Mat: 651230
  //   Arquitetura de Computadores I
  //   Pedro Henrique Lima Carvalho
endmodule

module Ram_1x1 (
  input  Addr,
  input  R_W,
  input  Clk,
  input  In,
  input  Clear,
  output Out
);

  wire and_1_out, j_k_ff_1_q, not_1_out;

  and and_1 (and_1_out, Addr, R_W, Clk);
  not not_1 (not_1_out, In);
  J_K_Flip_Flop j_k_ff_1 (.J(In), .clk(and_1_out), .K(not_1_out), .Q(j_k_ff_1_q), .reset(Clear));  // open: Qn, preset
  and and_2 (Out, Addr, j_k_ff_1_q);

  // Notes on the sheet:
  //   Mat: 651230
  //   Arquitetura de Computadores I
  //   Pedro Henrique Lima Carvalho
endmodule

module Ram_1x2 (
  input  Addr,
  input  R_W,
  input  Clk,
  input  [1:0] In,
  input  Clear,
  output [1:0] Out
);

  wire _0, _1;

  Ram_1x1 ram_1x1_1 (.Addr(Addr), .R_W(R_W), .Clk(Clk), .In(In[0]), .Clear(Clear), .Out(_0));
  Ram_1x1 ram_1x1_2 (.Addr(Addr), .R_W(R_W), .Clk(Clk), .In(In[1]), .Clear(Clear), .Out(_1));
  assign Out = {2{Addr}} & {_1, _0};  // AND_Gate and_1, 2 bits wide

  // Notes on the sheet:
  //   Mat: 651230
  //   Arquitetura de Computadores I
  //   Pedro Henrique Lima Carvalho
endmodule

module Ram_1x4_2de1x2 (
  input  Addr,
  input  R_W,
  input  Clk,
  input  [3:0] In,
  input  Clear,
  output [3:0] Out
);

  wire [1:0] ram_1x2_1_out, ram_1x2_2_out;

  Ram_1x2 ram_1x2_1 (.Addr(Addr), .R_W(R_W), .Clk(Clk), .In(In[1:0]), .Clear(Clear), .Out(ram_1x2_1_out));
  Ram_1x2 ram_1x2_2 (.Addr(Addr), .R_W(R_W), .Clk(Clk), .In(In[3:2]), .Clear(Clear), .Out(ram_1x2_2_out));
  assign Out = {4{Addr}} & {ram_1x2_2_out, ram_1x2_1_out};  // AND_Gate and_1, 4 bits wide

  // Notes on the sheet:
  //   Mat: 651230
  //   Arquitetura de Computadores I
  //   Pedro Henrique Lima Carvalho
endmodule

module Ram_1x8 (
  input  Addr,
  input  R_W,
  input  Clk,
  input  [7:0] in_4,
  input  Clear,
  output [7:0] out_6
);

  wire [3:0] ram_1x4_2de1x2_1_out, ram_1x4_2de1x2_2_out;

  Ram_1x4_2de1x2 ram_1x4_2de1x2_1 (
    .Addr(Addr), .R_W(R_W), .Clk(Clk), .In(in_4[3:0]), .Clear(Clear), .Out(ram_1x4_2de1x2_1_out));
  Ram_1x4_2de1x2 ram_1x4_2de1x2_2 (
    .Addr(Addr), .R_W(R_W), .Clk(Clk), .In(in_4[7:4]), .Clear(Clear), .Out(ram_1x4_2de1x2_2_out));
  Multiplexer #(.width(8), .enable("false")) multiplexer_1 (
    .in0({8{1'b0}}), .in1({ram_1x4_2de1x2_2_out, ram_1x4_2de1x2_1_out}), .out(out_6), .sel(Addr));

  // Notes on the sheet:
  //   Mat: 651230
  //   Arquitetura de Computadores I
  //   Pedro Henrique Lima Carvalho
endmodule

module Ram_4x8 (
  input  [1:0] in_1,
  input  R_W,
  input  Clk,
  input  [7:0] In,
  input  Clear,
  output [7:0] Out
);

  wire demultiplexer_1_out0, demultiplexer_1_out1, demultiplexer_1_out2, demultiplexer_1_out3;
  wire [7:0] ram_1x8_1_out_6, ram_1x8_2_out_6, ram_1x8_3_out_6, ram_1x8_4_out_6;

  Demultiplexer #(.select(2), .enable("false")) demultiplexer_1 (
    .out0(demultiplexer_1_out0), .out1(demultiplexer_1_out1), .out2(demultiplexer_1_out2),
    .out3(demultiplexer_1_out3), .in(1'b1), .sel(in_1));
  Ram_1x8 ram_1x8_1 (
    .Addr(demultiplexer_1_out0), .R_W(R_W), .Clk(Clk), .in_4(In), .Clear(Clear), .out_6(ram_1x8_1_out_6));
  Ram_1x8 ram_1x8_2 (
    .Addr(demultiplexer_1_out1), .R_W(R_W), .Clk(Clk), .in_4(In), .Clear(Clear), .out_6(ram_1x8_2_out_6));
  Ram_1x8 ram_1x8_3 (
    .Addr(demultiplexer_1_out2), .R_W(R_W), .Clk(Clk), .in_4(In), .Clear(Clear), .out_6(ram_1x8_3_out_6));
  Ram_1x8 ram_1x8_4 (
    .Addr(demultiplexer_1_out3), .R_W(R_W), .Clk(Clk), .in_4(In), .Clear(Clear), .out_6(ram_1x8_4_out_6));
  Multiplexer #(.select(2), .width(8), .enable("false")) multiplexer_1 (
    .in0(ram_1x8_1_out_6), .in1(ram_1x8_2_out_6), .in2(ram_1x8_3_out_6), .in3(ram_1x8_4_out_6), .out(Out),
    .sel(in_1));

  // Notes on the sheet:
  //   Mat: 651230
  //   Arquitetura de Computadores I
  //   Pedro Henrique Lima Carvalho
endmodule

module Ram_8x8 (
  input  [2:0] Addr,
  input  R_W,
  input  Clk,
  input  [7:0] In,
  input  Clear,
  output [7:0] Out
);

  wire Clk0, Clk1;
  wire [1:0] demultiplexer_1_out0, demultiplexer_1_out1;
  wire [7:0] ram_4x8_1_out, ram_4x8_2_out;

  Demultiplexer #(.width(2), .enable("false")) demultiplexer_1 (
    .out0(demultiplexer_1_out0), .out1(demultiplexer_1_out1), .in(Addr[1:0]), .sel(Addr[2]));
  Demultiplexer #(.enable("false")) demultiplexer_2 (.out0(Clk0), .out1(Clk1), .in(Clk), .sel(Addr[2]));
  Ram_4x8 ram_4x8_1 (.in_1(demultiplexer_1_out0), .R_W(R_W), .Clk(Clk0), .In(In), .Clear(Clear), .Out(ram_4x8_1_out));
  Ram_4x8 ram_4x8_2 (.in_1(demultiplexer_1_out1), .R_W(R_W), .Clk(Clk1), .In(In), .Clear(Clear), .Out(ram_4x8_2_out));
  Multiplexer #(.width(8), .enable("false")) multiplexer_1 (
    .in0(ram_4x8_1_out), .in1(ram_4x8_2_out), .out(Out), .sel(Addr[2]));

  // Notes on the sheet:
  //   Mat: 651230
  //   Arquitetura de Computadores I
  //   Pedro Henrique Lima Carvalho
endmodule
