// Logisim project Pedro_Carvalho_651230_Guia_13.circ as structural Verilog: 7 circuits, main circuit Exemplo 1
module Exemplo_1 (
  input  Clk,
  input  in,
  input  Clr,
  output out_4,
  output out_5,
  output out_6,
  output out_7,
  output out_8
);

  D_Flip_Flop d_ff_1 (.clk(Clk), .D(out_5), .Q(out_4), .reset(Clr));  // open: Qn, preset
  D_Flip_Flop d_ff_2 (.clk(Clk), .D(out_6), .Q(out_5), .reset(Clr));  // open: Qn, preset
  D_Flip_Flop d_ff_3 (.clk(Clk), .D(out_7), .Q(out_6), .reset(Clr));  // open: Qn, preset
  D_Flip_Flop d_ff_4 (.clk(Clk), .D(out_8), .Q(out_7), .reset(Clr));  // open: Qn, preset
  D_Flip_Flop d_ff_5 (.clk(Clk), .D(in), .Q(out_8), .reset(Clr));  // open: Qn, preset

  // Notes on the sheet:
  //   Arquitetura de Computadores I
  //   Pedro Henrique Lima Carvalho
  //   Guia 13 - Exercicio 1
endmodule

module Exemplo_2 (
  input  Clk,
  input  Clr,
  input  Load,
  input  in_4,
  input  in_5,
  input  in_6,
  input  in_7,
  input  in_8,
  output out_9,
  output out_10,
  output out_11,
  output out_12,
  output out_13
);

  wire and_1_out, and_2_out, and_3_out, and_4_out, and_5_out;

  D_Flip_Flop #(.Pre_Clr_Positions("LEGACY")) d_ff_1 (
    .clk(Clk), .D(out_10), .Q(out_9), .preset(and_1_out), .reset(Clr));  // open: Qn
  and and_1 (and_1_out, in_4, Load);
  and and_2 (and_2_out, in_5, Load);
  D_Flip_Flop #(.Pre_Clr_Positions("LEGACY")) d_ff_2 (
    .clk(Clk), .D(out_11), .Q(out_10), .preset(and_2_out), .reset(Clr));  // open: Qn
  D_Flip_Flop #(.Pre_Clr_Positions("LEGACY")) d_ff_3 (
    .clk(Clk), .D(out_12), .Q(out_11), .preset(and_3_out), .reset(Clr));  // open: Qn
  and and_3 (and_3_out, in_6, Load);
  D_Flip_Flop #(.Pre_Clr_Positions("LEGACY")) d_ff_4 (
    .clk(Clk), .D(out_13), .Q(out_12), .preset(and_4_out), .reset(Clr));  // open: Qn
  and and_4 (and_4_out, in_7, Load);
  and and_5 (and_5_out, in_8, Load);
  D_Flip_Flop #(.Pre_Clr_Positions("LEGACY")) d_ff_5 (
    .clk(Clk), .D(1'b0), .Q(out_13), .preset(and_5_out), .reset(Clr));  // open: Qn

  // Notes on the sheet:
  //   Arquitetura de Computadores I
  //   Pedro Henrique Lima Carvalho
  //   Guia 13 - Exercicio 2
endmodule

module Exemplo_3 (
  input  Clk,
  input  in,
  input  Clr,
  output out_4,
  output out_5,
  output out_6,
  output out_7,
  output out_8
);

  wire or_1_out;

  or or_1 (or_1_out, out_8, in);
  D_Flip_Flop d_ff_1 (.clk(Clk), .D(or_1_out), .Q(out_4), .reset(Clr));  // open: Qn, preset
  D_Flip_Flop d_ff_2 (.clk(Clk), .D(out_4), .Q(out_5), .reset(Clr));  // open: Qn, preset
  D_Flip_Flop d_ff_3 (.clk(Clk), .D(out_5), .Q(out_6), .reset(Clr));  // open: Qn, preset
  D_Flip_Flop d_ff_4 (.clk(Clk), .D(out_6), .Q(out_7), .reset(Clr));  // open: Qn, preset
  D_Flip_Flop d_ff_5 (.clk(Clk), .D(out_7), .Q(out_8), .reset(Clr));  // open: Qn, preset

  // Notes on the sheet:
  //   Arquitetura de Computadores I
  //   Pedro Henrique Lima Carvalho
  //   Guia 13 - Exercicio 3
endmodule

module Exemplo_4 (
  input  Clk,
  input  in,
  input  Clr,
  output out_4,
  output out_5,
  output out_6,
  output out_7,
  output out_8
);

  wire d_ff_1_qn, or_1_out;

  D_Flip_Flop d_ff_1 (.clk(Clk), .D(out_5), .Q(out_4), .Qn(d_ff_1_qn), .reset(Clr));  // open: preset
  or or_1 (or_1_out, d_ff_1_qn, in);
  D_Flip_Flop d_ff_2 (.clk(Clk), .D(out_6), .Q(out_5), .reset(Clr));  // open: Qn, preset
  D_Flip_Flop d_ff_3 (.clk(Clk), .D(out_7), .Q(out_6), .reset(Clr));  // open: Qn, preset
  D_Flip_Flop d_ff_4 (.clk(Clk), .D(out_8), .Q(out_7), .reset(Clr));  // open: Qn, preset
  D_Flip_Flop d_ff_5 (.clk(Clk), .D(or_1_out), .Q(out_8), .reset(Clr));  // open: Qn, preset

  // Notes on the sheet:
  //   Arquitetura de Computadores I
  //   Pedro Henrique Lima Carvalho
  //   Guia 13 - Exercicio 4
endmodule

module Exemplo_5 (
  input  Clk,
  input  Clr,
  input  Load,
  input  in_4,
  input  in_5,
  input  in_6,
  input  in_7,
  input  in_8,
  output out_9,
  output out_10,
  output out_11,
  output out_12,
  output out_13
);

  wire and_1_out, and_2_out, and_3_out, and_4_out, and_5_out;

  and and_1 (and_1_out, in_4, Load);
  D_Flip_Flop #(.Pre_Clr_Positions("LEGACY")) d_ff_1 (
    .clk(Clk), .D(1'b0), .Q(out_9), .preset(and_1_out), .reset(Clr));  // open: Qn
  and and_2 (and_2_out, in_5, Load);
  D_Flip_Flop #(.Pre_Clr_Positions("LEGACY")) d_ff_2 (
    .clk(Clk), .D(out_9), .Q(out_10), .preset(and_2_out), .reset(Clr));  // open: Qn
  D_Flip_Flop #(.Pre_Clr_Positions("LEGACY")) d_ff_3 (
    .clk(Clk), .D(out_10), .Q(out_11), .preset(and_3_out), .reset(Clr));  // open: Qn
  and and_3 (and_3_out, in_6, Load);
  and and_4 (and_4_out, in_7, Load);
  D_Flip_Flop #(.Pre_Clr_Positions("LEGACY")) d_ff_4 (
    .clk(Clk), .D(out_11), .Q(out_12), .preset(and_4_out), .reset(Clr));  // open: Qn
  D_Flip_Flop #(.Pre_Clr_Positions("LEGACY")) d_ff_5 (
    .clk(Clk), .D(out_12), .Q(out_13), .preset(and_5_out), .reset(Clr));  // open: Qn
  and and_5 (and_5_out, in_8, Load);

  // Notes on the sheet:
  //   Arquitetura de Computadores I
  //   Pedro Henrique Lima Carvalho
  //   Guia 13 - Exercicio 5
endmodule

module Exemplo_6 (
  input  Clk,
  input  Clr,
  input  Load,
  input  in_4,
  input  in_5,
  input  in_6,
  input  in_7,
  input  in_8,
  output out_9,
  output out_10,
  output out_11,
  output out_12,
  output out_13
);

  wire and_1_out, and_2_out, and_3_out, and_4_out, and_5_out;

  and and_1 (and_1_out, in_4, Load);
  D_Flip_Flop #(.Pre_Clr_Positions("LEGACY")) d_ff_1 (
    .clk(Clk), .D(out_10), .Q(out_9), .preset(and_1_out), .reset(Clr));  // open: Qn
  and and_2 (and_2_out, in_5, Load);
  D_Flip_Flop #(.Pre_Clr_Positions("LEGACY")) d_ff_2 (
    .clk(Clk), .D(out_11), .Q(out_10), .preset(and_2_out), .reset(Clr));  // open: Qn
  D_Flip_Flop #(.Pre_Clr_Positions("LEGACY")) d_ff_3 (
    .clk(Clk), .D(out_12), .Q(out_11), .preset(and_3_out), .reset(Clr));  // open: Qn
  and and_3 (and_3_out, in_6, Load);
  and and_4 (and_4_out, in_7, Load);
  D_Flip_Flop #(.Pre_Clr_Positions("LEGACY")) d_ff_4 (
    .clk(Clk), .D(out_13), .Q(out_12), .preset(and_4_out), .reset(Clr));  // open: Qn
  D_Flip_Flop #(.Pre_Clr_Positions("LEGACY")) d_ff_5 (
    .clk(Clk), .D(out_9), .Q(out_13), .preset(and_5_out), .reset(Clr));  // open: Qn
  and and_5 (and_5_out, in_8, Load);

  // Notes on the sheet:
  //   Arquitetura de Computadores I
  //   Pedro Henrique Lima Carvalho
  //   Guia 13 - Exercicio 6
endmodule

module Exemplo_7 (
  input  Clk,
  input  Clr,
  input  Load,
  input  in_4,
  input  in_5,
  input  in_6,
  input  in_7,
  input  in_8,
  output out_9,
  output out_10,
  output out_11,
  output out_12,
  output out_13
);

  wire and_1_out, and_2_out, and_3_out, and_4_out, and_5_out, d_ff_5_qn;

  and and_1 (and_1_out, in_4, Load);
  D_Flip_Flop #(.Pre_Clr_Positions("LEGACY")) d_ff_1 (
    .clk(Clk), .D(d_ff_5_qn), .Q(out_9), .preset(and_1_out), .reset(Clr));  // open: Qn
  and and_2 (and_2_out, in_5, Load);
  D_Flip_Flop #(.Pre_Clr_Positions("LEGACY")) d_ff_2 (
    .clk(Clk), .D(out_9), .Q(out_10), .preset(and_2_out), .reset(Clr));  // open: Qn
  D_Flip_Flop #(.Pre_Clr_Positions("LEGACY")) d_ff_3 (
    .clk(Clk), .D(out_10), .Q(out_11), .preset(and_3_out), .reset(Clr));  // open: Qn
  and and_3 (and_3_out, in_6, Load);
  and and_4 (and_4_out, in_7, Load);
  D_Flip_Flop #(.Pre_Clr_Positions("LEGACY")) d_ff_4 (
    .clk(Clk), .D(out_11), .Q(out_12), .preset(and_4_out), .reset(Clr));  // open: Qn
  D_Flip_Flop #(.Pre_Clr_Positions("LEGACY")) d_ff_5 (
    .clk(Clk), .D(out_12), .Q(out_13), .Qn(d_ff_5_qn), .preset(and_5_out), .reset(Clr));
  and and_5 (and_5_out, in_8, Load);

  // Notes on the sheet:
  //   Arquitetura de Computadores I
  //   Pedro Henrique Lima Carvalho
  //   Guia 13 - Exercicio 7
endmodule
