// Logisim project Pedro_Carvalho_651230_Guia_14.circ as structural Verilog: 7 circuits, main circuit Exemplo 1
module Exemplo_1 (
  input  Pulse,
  input  On_Off,
  input  Clear
);

  wire j_k_ff_1_q, j_k_ff_2_q, j_k_ff_3_q, j_k_ff_4_q, j_k_ff_5_q;

  // Probe on j_k_ff_1_q
  J_K_Flip_Flop j_k_ff_1 (.J(On_Off), .clk(j_k_ff_2_q), .K(On_Off), .Q(j_k_ff_1_q), .reset(Clear));  // open: Qn, preset
  // Probe on j_k_ff_2_q
  J_K_Flip_Flop j_k_ff_2 (.J(On_Off), .clk(j_k_ff_3_q), .K(On_Off), .Q(j_k_ff_2_q), .reset(Clear));  // open: Qn, preset
  // Probe on j_k_ff_3_q
  J_K_Flip_Flop j_k_ff_3 (.J(On_Off), .clk(j_k_ff_4_q), .K(On_Off), .Q(j_k_ff_3_q), .reset(Clear));  // open: Qn, preset
  // Probe on j_k_ff_4_q
  J_K_Flip_Flop j_k_ff_4 (.J(On_Off), .clk(j_k_ff_5_q), .K(On_Off), .Q(j_k_ff_4_q), .reset(Clear));  // open: Qn, preset
  // Probe on j_k_ff_5_q
  J_K_Flip_Flop j_k_ff_5 (.J(On_Off), .clk(Pulse), .K(On_Off), .Q(j_k_ff_5_q), .reset(Clear));  // open: Qn, preset

  // Notes on the sheet:
  //   Guia 14
  //   Arquitetura de Computadores I
  //   Pedro Henrique Lima Carvalho
  //   Mat: 651230
endmodule

module Exemplo_2 (
  input  Pulse,
  input  On_Off,
  input  Clear
);

  wire j_k_ff_1_q, j_k_ff_2_q, j_k_ff_2_qn, j_k_ff_3_q, j_k_ff_3_qn, j_k_ff_4_q, j_k_ff_4_qn, j_k_ff_5_q,
       j_k_ff_5_qn;

  // Probe on j_k_ff_1_q
  J_K_Flip_Flop j_k_ff_1 (
    .J(On_Off), .clk(j_k_ff_2_qn), .K(On_Off), .Q(j_k_ff_1_q), .reset(Clear));  // open: Qn, preset
  // Probe on j_k_ff_2_q
  J_K_Flip_Flop j_k_ff_2 (
    .J(On_Off), .clk(j_k_ff_3_qn), .K(On_Off), .Q(j_k_ff_2_q), .Qn(j_k_ff_2_qn), .reset(Clear));  // open: preset
  // Probe on j_k_ff_3_q
  J_K_Flip_Flop j_k_ff_3 (
    .J(On_Off), .clk(j_k_ff_4_qn), .K(On_Off), .Q(j_k_ff_3_q), .Qn(j_k_ff_3_qn), .reset(Clear));  // open: preset
  // Probe on j_k_ff_4_q
  J_K_Flip_Flop j_k_ff_4 (
    .J(On_Off), .clk(j_k_ff_5_qn), .K(On_Off), .Q(j_k_ff_4_q), .Qn(j_k_ff_4_qn), .reset(Clear));  // open: preset
  // Probe on j_k_ff_5_q
  J_K_Flip_Flop j_k_ff_5 (
    .J(On_Off), .clk(Pulse), .K(On_Off), .Q(j_k_ff_5_q), .Qn(j_k_ff_5_qn), .reset(Clear));  // open: preset

  // Notes on the sheet:
  //   Arquitetura de Computadores I
  //   Guia 14
  //   Pedro Henrique Lima Carvalho
  //   Mat: 651230
endmodule

module Exemplo_3 (
  input  Pulse,
  input  On_Off,
  input  Clear
);

  wire and_1_out, j_k_ff_1_q, j_k_ff_2_q, j_k_ff_2_qn, j_k_ff_3_q, j_k_ff_3_qn, j_k_ff_4_q, j_k_ff_4_qn,
       j_k_ff_5_q, j_k_ff_5_qn, not_1_out, or_1_out;

  // Probe on j_k_ff_1_q
  J_K_Flip_Flop j_k_ff_1 (
    .J(On_Off), .clk(j_k_ff_2_qn), .K(On_Off), .Q(j_k_ff_1_q), .reset(or_1_out));  // open: Qn, preset
  or or_1 (or_1_out, Clear, and_1_out);
  not not_1 (not_1_out, j_k_ff_3_q);
  and and_1 (and_1_out, j_k_ff_2_q, not_1_out, j_k_ff_4_q, j_k_ff_5_q);
  // Probe on j_k_ff_2_q
  J_K_Flip_Flop j_k_ff_2 (
    .J(On_Off), .clk(j_k_ff_3_qn), .K(On_Off), .Q(j_k_ff_2_q), .Qn(j_k_ff_2_qn), .reset(or_1_out));  // open: preset
  // Probe on j_k_ff_3_q
  J_K_Flip_Flop j_k_ff_3 (
    .J(On_Off), .clk(j_k_ff_4_qn), .K(On_Off), .Q(j_k_ff_3_q), .Qn(j_k_ff_3_qn), .reset(or_1_out));  // open: preset
  // Probe on j_k_ff_4_q
  J_K_Flip_Flop j_k_ff_4 (
    .J(On_Off), .clk(j_k_ff_5_qn), .K(On_Off), .Q(j_k_ff_4_q), .Qn(j_k_ff_4_qn), .reset(or_1_out));  // open: preset
  // Probe on j_k_ff_5_q
  J_K_Flip_Flop j_k_ff_5 (
    .J(On_Off), .clk(Pulse), .K(On_Off), .Q(j_k_ff_5_q), .Qn(j_k_ff_5_qn), .reset(or_1_out));  // open: preset

  // Notes on the sheet:
  //   Arquitetura de Computadores I
  //   Guia 14
  //   Pedro Henrique Lima Carvalho
  //   Mat: 651230
endmodule

module Exemplo_4 (
  input  Pulse,
  input  On_Off
);

  wire and_1_out, j_k_ff_1_q, j_k_ff_1_qn, j_k_ff_2_q, j_k_ff_2_qn, j_k_ff_3_q, j_k_ff_3_qn, j_k_ff_4_q,
       j_k_ff_4_qn, j_k_ff_5_q, j_k_ff_5_qn, not_1_out, not_2_out, not_3_out, not_4_out, or_1_out;

  not not_1 (not_1_out, On_Off);
  // Probe on j_k_ff_5_q
  J_K_Flip_Flop #(.Pre_Clr_Positions("BELOW_ABOVE")) j_k_ff_1 (
    .J(On_Off), .clk(Pulse), .K(On_Off), .Q(j_k_ff_1_q), .Qn(j_k_ff_1_qn), .preset(or_1_out));  // open: reset
  or or_1 (or_1_out, not_1_out, and_1_out);
  not not_2 (not_2_out, j_k_ff_1_qn);
  not not_3 (not_3_out, j_k_ff_3_qn);
  and and_1 (and_1_out, not_2_out, j_k_ff_2_qn, not_3_out, j_k_ff_4_qn, not_4_out);
  not not_4 (not_4_out, j_k_ff_5_qn);
  // Probe on j_k_ff_4_q
  J_K_Flip_Flop #(.Pre_Clr_Positions("BELOW_ABOVE")) j_k_ff_2 (
    .J(On_Off), .clk(j_k_ff_1_q), .K(On_Off), .Q(j_k_ff_2_q), .Qn(j_k_ff_2_qn), .preset(or_1_out));  // open: reset
  // Probe on j_k_ff_3_q
  J_K_Flip_Flop #(.Pre_Clr_Positions("BELOW_ABOVE")) j_k_ff_3 (
    .J(On_Off), .clk(j_k_ff_2_q), .K(On_Off), .Q(j_k_ff_3_q), .Qn(j_k_ff_3_qn), .preset(or_1_out));  // open: reset
  // Probe on j_k_ff_2_q
  J_K_Flip_Flop #(.Pre_Clr_Positions("BELOW_ABOVE")) j_k_ff_4 (
    .J(On_Off), .clk(j_k_ff_3_q), .K(On_Off), .Q(j_k_ff_4_q), .Qn(j_k_ff_4_qn), .preset(or_1_out));  // open: reset
  // Probe on j_k_ff_1_q
  J_K_Flip_Flop #(.Pre_Clr_Positions("BELOW_ABOVE")) j_k_ff_5 (
    .J(On_Off), .clk(j_k_ff_4_q), .K(On_Off), .Q(j_k_ff_5_q), .Qn(j_k_ff_5_qn), .preset(or_1_out));  // open: reset

  // Notes on the sheet:
  //   Guia 14
  //   Arquitetura de Computadores I
  //   Pedro Henrique Lima Carvalho
  //   Mat: 651230
endmodule

module Exemplo_5 (
  input  Pulse,
  input  in_2
);

  wire and_1_out, not_1_out, or_1_out, t_ff_1_q, t_ff_1_qn, t_ff_2_q, t_ff_2_qn, t_ff_3_q, t_ff_3_qn,
       t_ff_4_q;

  not not_1 (not_1_out, in_2);
  or or_1 (or_1_out, not_1_out, and_1_out);
  and and_1 (and_1_out, t_ff_2_q, t_ff_4_q);
  // Probe on t_ff_4_q
  T_Flip_Flop t_ff_1 (.clk(Pulse), .T(in_2), .Q(t_ff_1_q), .Qn(t_ff_1_qn), .reset(or_1_out));  // open: preset
  // Probe on t_ff_3_q
  T_Flip_Flop t_ff_2 (.clk(t_ff_1_qn), .T(in_2), .Q(t_ff_2_q), .Qn(t_ff_2_qn), .reset(or_1_out));  // open: preset
  // Probe on t_ff_2_q
  T_Flip_Flop t_ff_3 (.clk(t_ff_2_qn), .T(in_2), .Q(t_ff_3_q), .Qn(t_ff_3_qn), .reset(or_1_out));  // open: preset
  // Probe on t_ff_1_q
  T_Flip_Flop t_ff_4 (.clk(t_ff_3_qn), .T(in_2), .Q(t_ff_4_q), .reset(or_1_out));  // open: Qn, preset

  // Notes on the sheet:
  //   Guia 14
  //   Arquitetura de Computadores I
  //   Pedro Henrique Lima Carvalho
  //   Mat: 651230
endmodule

module Exemplo_6 (
  input  Pulse,
  input  Clear
);

  wire j_k_ff_1_q, j_k_ff_2_q, j_k_ff_3_q, j_k_ff_4_q, j_k_ff_5_q, not_1_out, not_2_out, not_3_out,
       not_4_out, not_5_out;

  J_K_Flip_Flop #(.Pre_Clr_Positions("BELOW_ABOVE")) j_k_ff_1 (
    .J(j_k_ff_5_q), .clk(Pulse), .K(not_1_out), .Q(j_k_ff_1_q), .preset(Clear));  // open: Qn, reset
  not not_1 (not_1_out, j_k_ff_5_q);
  not not_2 (not_2_out, j_k_ff_1_q);
  J_K_Flip_Flop j_k_ff_2 (
    .J(j_k_ff_1_q), .clk(Pulse), .K(not_2_out), .Q(j_k_ff_2_q), .reset(Clear));  // open: Qn, preset
  not not_3 (not_3_out, j_k_ff_2_q);
  J_K_Flip_Flop j_k_ff_3 (
    .J(j_k_ff_2_q), .clk(Pulse), .K(not_3_out), .Q(j_k_ff_3_q), .reset(Clear));  // open: Qn, preset
  J_K_Flip_Flop j_k_ff_4 (
    .J(j_k_ff_3_q), .clk(Pulse), .K(not_4_out), .Q(j_k_ff_4_q), .reset(Clear));  // open: Qn, preset
  not not_4 (not_4_out, j_k_ff_3_q);
  not not_5 (not_5_out, j_k_ff_4_q);
  J_K_Flip_Flop j_k_ff_5 (
    .J(j_k_ff_4_q), .clk(Pulse), .K(not_5_out), .Q(j_k_ff_5_q), .reset(Clear));  // open: Qn, preset

  // Notes on the sheet:
  //   Arquitetura de Computadores I
  //   Guia 14
  //   Pedro Henrique Lima Carvalho
  //   Mat: 651230
endmodule

module Exemplo_7 (
  input  Pulse,
  input  Clear
);

  wire j_k_ff_1_q, j_k_ff_2_q, j_k_ff_3_q, j_k_ff_4_q, j_k_ff_5_qn, not_1_out, not_2_out, not_3_out,
       not_4_out, not_5_out;

  J_K_Flip_Flop j_k_ff_1 (
    .J(j_k_ff_5_qn), .clk(Pulse), .K(not_1_out), .Q(j_k_ff_1_q), .reset(Clear));  // open: Qn, preset
  not not_1 (not_1_out, j_k_ff_5_qn);
  not not_2 (not_2_out, j_k_ff_1_q);
  J_K_Flip_Flop j_k_ff_2 (
    .J(j_k_ff_1_q), .clk(Pulse), .K(not_2_out), .Q(j_k_ff_2_q), .reset(Clear));  // open: Qn, preset
  not not_3 (not_3_out, j_k_ff_2_q);
  J_K_Flip_Flop j_k_ff_3 (
    .J(j_k_ff_2_q), .clk(Pulse), .K(not_3_out), .Q(j_k_ff_3_q), .reset(Clear));  // open: Qn, preset
  J_K_Flip_Flop j_k_ff_4 (
    .J(j_k_ff_3_q), .clk(Pulse), .K(not_4_out), .Q(j_k_ff_4_q), .reset(Clear));  // open: Qn, preset
  not not_4 (not_4_out, j_k_ff_3_q);
  not not_5 (not_5_out, j_k_ff_4_q);
  J_K_Flip_Flop j_k_ff_5 (
    .J(j_k_ff_4_q), .clk(Pulse), .K(not_5_out), .Qn(j_k_ff_5_qn), .reset(Clear));  // open: Q, preset

  // Notes on the sheet:
  //   Arquitetura de Computadores I
  //   Guia 14
  //   Pedro Henrique Lima Carvalho
  //   Mat: 651230
endmodule
